// Logisim project ALU.circ as structural Verilog: 1 circuit, main circuit SIMPLE_ALU
module SIMPLE_ALU (
  input  [7:0] BUS_IN_A,
  input  [7:0] BUS_IN_B,
  input  SUBSTRACT,
  input  E0,
  output CARRY,
  output ZERO,
  output BORROW,
  output [7:0] BUS_OUT
);

  wire adder_1_cout, nor_1_out, or_1_out, or_2_out, subtractor_1_bout;
  wire [7:0] adder_1_out, controlled_buffer_1_out, subtractor_1_out;

  Adder adder_1 (.a(BUS_IN_A), .b(BUS_IN_B), .out(adder_1_out), .cin(SUBSTRACT), .cout(adder_1_cout));
  Subtractor subtractor_1 (.a(BUS_IN_A), .b(BUS_IN_B), .out(subtractor_1_out), .bout(subtractor_1_bout));  // open: bin
  or or_1 (or_1_out, SUBSTRACT, E0);
  assign controlled_buffer_1_out = E0 ? adder_1_out : 8'bz;  // Controlled_Buffer controlled_buffer_1
  assign CARRY = or_1_out ? adder_1_cout : 1'bz;  // Controlled_Buffer controlled_buffer_2
  assign BORROW = or_1_out ? subtractor_1_bout : 1'bz;  // Controlled_Buffer controlled_buffer_3
  assign controlled_buffer_1_out = SUBSTRACT ? subtractor_1_out : 8'bz;  // Controlled_Buffer controlled_buffer_4
  assign BUS_OUT = or_2_out ? controlled_buffer_1_out : 8'bz;  // Controlled_Buffer controlled_buffer_5
  or or_2 (or_2_out, SUBSTRACT, E0);
  nor nor_1 (nor_1_out, controlled_buffer_1_out[0], controlled_buffer_1_out[1], controlled_buffer_1_out[2], controlled_buffer_1_out[3], controlled_buffer_1_out[4], controlled_buffer_1_out[5], controlled_buffer_1_out[6], controlled_buffer_1_out[7]);
  assign ZERO = or_1_out ? nor_1_out : 1'bz;  // Controlled_Buffer controlled_buffer_6
endmodule
