// Logisim project BCDto7Segment.circ as structural Verilog: 1 circuit, main circuit main
module main (
  input  [7:0] in_1,
  output [3:0] L_0_667fbc26,
  output [3:0] L_1_7d65beac,
  output [3:0] L_2_df72e25f
);

  wire [7:4] divider_1_rem;

  Divider divider_1 (
    .a(in_1), .b(8'ha), .out({L_2_df72e25f, L_1_7d65beac}), .upper({8{1'b0}}),
    .rem({divider_1_rem, L_0_667fbc26}));
endmodule
