// Logisim project BCDto7Segment_evo.circ as structural Verilog: 1 circuit, main circuit main
module main (
  input  [31:0] in_1,
  output [3:0] L_0_667fbc26,
  output [3:0] L_1_7d65beac,
  output [3:0] L_2_df72e25f,
  output [3:0] L_3_63c192f7,
  output [3:0] L_4_29344f04,
  output [3:0] L_5_7fd0462a,
  output [3:0] L_6_c951fa01,
  output [3:0] L_7_ee07fd4f
);

  wire [3:0] divider_1_out;
  wire [31:4] divider_1_rem;

  Divider #(.width(32)) divider_1 (
    .a(in_1), .b(32'ha),
    .out({L_7_ee07fd4f, L_6_c951fa01, L_5_7fd0462a, L_4_29344f04, L_3_63c192f7, L_2_df72e25f, L_1_7d65beac, divider_1_out}),
    .upper({32{1'b0}}), .rem({divider_1_rem, L_0_667fbc26}));
endmodule
