// Logisim project BCDto7Segment_pre.circ as structural Verilog: 1 circuit, main circuit main
module main (
  input  [31:0] IN,
  input  in_2,
  output [3:0] _0,
  output [3:0] _1,
  output [3:0] _2,
  output [3:0] _3,
  output [3:0] _4,
  output [3:0] _5,
  output [3:0] _6,
  output [3:0] _7,
  output COUT
);

  wire and_1_out;
  wire [3:0] counter_2_q;
  wire [31:0] divider_1_out, divider_1_rem;
  wire [31:4] counter_1_q;

  Divider #(.width(32)) divider_1 (.a(IN), .b(32'ha), .out(divider_1_out), .upper({32{1'b0}}), .rem(divider_1_rem));
  Counter #(.width(32), .max('ha)) counter_1 (
    .load(1'b1), .D(divider_1_rem), .count(1'b0), .Q({counter_1_q, _0}), .clk(in_2), .clr(and_1_out));  // open: carry
  and and_1 (and_1_out, _0[3], _0[1]);
  Counter #(.width(32), .max('hffffffff)) counter_2 (
    .load(1'b1), .D(divider_1_out), .count(1'b0), .Q({counter_2_q, _7, _6, _5, _4, _3, _2, _1}), .clk(in_2));  // open: carry, clr
endmodule
