// Logisim project MAR_DEC.circ as structural Verilog: 1 circuit, main circuit main
module main (
  input  JMP,
  input  INS_INC,
  input  CLK,
  input  [7:0] BUS_IN,
  input  in_5,
  output [7:0] BUS_OUT
);

  wire decoder_1_out15;
  wire [7:0] counter_1_q;

  Counter counter_1 (
    .clr(decoder_1_out15), .load(JMP), .up(INS_INC), .count(INS_INC), .clk(CLK), .D(BUS_IN), .Q(counter_1_q));  // open: carry
  Decoder #(.select(4)) decoder_1 (
    .out15(decoder_1_out15), .sel(counter_1_q[3:0]), .en(1'b1));  // open: out0, out1, out2, out3, out4, out5, out6, out7, out8, out9, out10, out11, out12, out13, out14
  assign BUS_OUT = in_5 ? counter_1_q : 8'bz;  // Controlled_Buffer controlled_buffer_1
endmodule
