// Logisim project ALLTOGETHER.circ as structural Verilog: 1 circuit, main circuit main
// STACK,PC,IR
module main (
  input  [7:0] BUSIN,
  input  C_plus_plus,
  input  C_minus_minus,
  input  LR0,
  input  LR2,
  input  LRO,
  input  CO,
  input  MI0,
  input  J0,
  input  MI2,
  input  J2,
  input  MII,
  input  CE,
  input  II,
  input  CLK,
  output [7:0] BUSOUT,
  output [7:0] RAM2,
  output [7:0] RAM1,
  output [7:0] RAM0,
  output [7:0] IRO
);

  wire decoder_1_out4, decoder_1_out5, decoder_1_out6, decoder_1_out7, main_1_p1, not_1_out, or_1_out;
  wire [7:0] controlled_buffer_1_out, controlled_buffer_2_out, controlled_buffer_3_out, main_1_p11,
       main_1_p12, main_1_p13, main_2_out1, main_2_out2, main_2_out3;

  not not_1 (not_1_out, LRO);
  assign controlled_buffer_1_out = not_1_out ? BUSIN : 8'bz;  // Controlled_Buffer controlled_buffer_1
  assign controlled_buffer_2_out = not_1_out ? BUSIN : 8'bz;  // Controlled_Buffer controlled_buffer_2
  assign controlled_buffer_3_out = not_1_out ? BUSIN : 8'bz;  // Controlled_Buffer controlled_buffer_3
  assign controlled_buffer_3_out = LRO ? main_1_p13 : 8'bz;  // Controlled_Buffer controlled_buffer_4
  assign controlled_buffer_1_out = LRO ? main_1_p11 : 8'bz;  // Controlled_Buffer controlled_buffer_5
  assign controlled_buffer_2_out = LRO ? main_1_p12 : 8'bz;  // Controlled_Buffer controlled_buffer_6
  // STACK_main main_1: pin names not known; wires that end beside it: main_1_p1, main_1_p1, BUSIN, C_plus_plus, C_minus_minus, BUSIN, CLK, LRO, LR2, LR0, main_1_p11, main_1_p12, main_1_p13
  COUNTER_main main_2 (
    .IN3(controlled_buffer_1_out), .IN2(controlled_buffer_2_out), .IN1(controlled_buffer_3_out), .CE(CE),
    .CO(CO), .J2(J2), .J0(J0), .CLK(CLK), .OUT3(main_2_out3), .OUT2(main_2_out2), .OUT1(main_2_out1));
  IR_main main_3 (.in_1(BUSIN), .II(II), .CLK(CLK), .out_4(IRO));
  assign BUSOUT = decoder_1_out6 ? main_2_out2 : 8'bz;  // Controlled_Buffer controlled_buffer_7
  assign BUSOUT = decoder_1_out7 ? main_2_out3 : 8'bz;  // Controlled_Buffer controlled_buffer_8
  assign BUSOUT = or_1_out ? main_2_out1 : 8'bz;  // Controlled_Buffer controlled_buffer_9
  MAR_main main_4 (
    .IN2(main_2_out3), .IN1(main_2_out2), .IN0(main_2_out1), .MI2(MI2), .MI0(MI0), .MII(MII), .CLK(CLK),
    .RAM2(RAM2), .RAM1(RAM1), .RAM0(RAM0));
  Decoder #(.select(3)) decoder_1 (
    .out4(decoder_1_out4), .out5(decoder_1_out5), .out6(decoder_1_out6), .out7(decoder_1_out7),
    .sel({CO, J2, J0}), .en(1'b1));  // open: out0, out1, out2, out3
  or or_1 (or_1_out, decoder_1_out4, decoder_1_out5);
endmodule
