// Logisim project COUNTER.circ as structural Verilog: 1 circuit, main circuit main
module main (
  input  [7:0] IN3,
  input  [7:0] IN2,
  input  [7:0] IN1,
  input  CE,
  input  CO,
  input  J2,
  input  J0,
  input  CLK,
  output [7:0] OUT3,
  output [7:0] OUT2,
  output [7:0] OUT1
);

  wire and_1_out, and_2_out, counter_2_carry, counter_3_carry, decoder_1_out1, decoder_1_out2,
       decoder_1_out3, decoder_1_out4, decoder_1_out5, decoder_1_out6, decoder_1_out7, not_1_out, not_2_out,
       not_3_out, or_1_out, or_2_out, or_3_out;
  wire [7:0] counter_1_q, counter_2_q, counter_3_q;

  and and_1 (and_1_out, CE, counter_2_carry);
  and and_2 (and_2_out, CE, counter_3_carry);
  Decoder #(.select(3)) decoder_1 (
    .out1(decoder_1_out1), .out2(decoder_1_out2), .out3(decoder_1_out3), .out4(decoder_1_out4),
    .out5(decoder_1_out5), .out6(decoder_1_out6), .out7(decoder_1_out7), .sel({CO, J2, J0}), .en(1'b1));  // open: out0
  Counter counter_1 (
    .load(decoder_1_out3), .D(IN3), .count(and_1_out), .Q(counter_1_q), .clk(CLK), .clr(1'b0));  // open: carry
  Counter counter_2 (
    .load(decoder_1_out2), .D(IN2), .count(and_2_out), .Q(counter_2_q), .carry(counter_2_carry), .clk(CLK),
    .clr(1'b0));
  Counter counter_3 (
    .load(decoder_1_out1), .D(IN1), .count(CE), .Q(counter_3_q), .carry(counter_3_carry), .clk(CLK),
    .clr(1'b0));
  or or_1 (or_1_out, decoder_1_out7, decoder_1_out4);
  not not_1 (not_1_out, or_1_out);
  assign OUT3 = not_1_out ? IN3 : 8'bz;  // Controlled_Buffer controlled_buffer_1
  assign OUT3 = or_1_out ? counter_1_q : 8'bz;  // Controlled_Buffer controlled_buffer_2
  not not_2 (not_2_out, or_2_out);
  assign OUT2 = not_2_out ? IN2 : 8'bz;  // Controlled_Buffer controlled_buffer_3
  assign OUT2 = or_2_out ? counter_2_q : 8'bz;  // Controlled_Buffer controlled_buffer_4
  not not_3 (not_3_out, or_3_out);
  assign OUT1 = not_3_out ? IN1 : 8'bz;  // Controlled_Buffer controlled_buffer_5
  assign OUT1 = or_3_out ? counter_3_q : 8'bz;  // Controlled_Buffer controlled_buffer_6
  or or_2 (or_2_out, decoder_1_out6, decoder_1_out4);
  or or_3 (or_3_out, decoder_1_out5, decoder_1_out4);
endmodule
