// Logisim project IR.circ as structural Verilog: 1 circuit, main circuit main
module main (
  input  [7:0] in_1,
  input  II,
  input  CLK,
  output [7:0] out_4
);

  Register register_1 (.D(in_1), .en(II), .Q(out_4), .clk(CLK), .clr(1'b0));
endmodule
