// Logisim project RAM.circ as structural Verilog: 1 circuit, main circuit main
module main (
  input  [7:0] BUS1X,
  input  [7:0] BUS1M,
  input  [7:0] BUS1L,
  input  RI,
  input  RO,
  input  CLK,
  input  [7:0] DATA,
  output [7:0] BUSO
);

  wire or_1_out;

  or or_1 (or_1_out, RI, RO);
  RAM #(.addrWidth(24), .bus("separate")) ram_1 (
    .addr({BUS1X, BUS1M, BUS1L}), .din(DATA), .data(BUSO), .str(RI), .sel(or_1_out), .clk(CLK), .ld(RO),
    .clr(1'b0));

  // Notes on the sheet:
  //   24 BIT PLAIN RAM!!!!
endmodule
