// Logisim project clock.circ as structural Verilog: 1 circuit, main circuit main
module main (
  input  HALT,
  input  PULSE,
  output CLK,
  output NCLK
);

  wire and_1_out, buffer_1_out, clock_1_out, not_1_out;

  buf buffer_1 (buffer_1_out, clock_1_out);
  Clock clock_1 (.out(clock_1_out));
  not not_1 (not_1_out, HALT);
  and and_1 (and_1_out, buffer_1_out, not_1_out);
  or or_1 (CLK, and_1_out, PULSE);
  not not_2 (NCLK, CLK);
endmodule
