// Logisim project REG16.circ as structural Verilog: 1 circuit, main circuit main
module main (
  input  E,
  input  X,
  input  H,
  input  L,
  input  [31:0] BUS_IN,
  input  A,
  input  SHA,
  input  LDA,
  input  CLA,
  input  B,
  input  SHB,
  input  LDB,
  input  CLB,
  input  C,
  input  SHC,
  input  LDC,
  input  CLC,
  input  D,
  input  SHD,
  input  LDD,
  input  CLD,
  input  CLK,
  output [31:0] BUS_OUT
);

  wire and_1_out, and_2_out, and_3_out, and_4_out, and_5_out, and_6_out, and_7_out, and_8_out, and_9_out,
       and_10_out, and_11_out, and_12_out, and_13_out, and_14_out, and_15_out, and_16_out, and_17_out,
       and_18_out, and_19_out, and_20_out, and_21_out, and_22_out, and_23_out, and_24_out, and_25_out,
       and_26_out, and_27_out, and_28_out, and_29_out, and_30_out, and_31_out, and_32_out, and_33_out,
       and_34_out, and_35_out, and_36_out, and_37_out, and_38_out, and_39_out, and_40_out, and_41_out,
       and_42_out, and_43_out, and_44_out, and_45_out, and_46_out, and_47_out, and_48_out, and_49_out,
       and_50_out, and_51_out, and_52_out;
  wire [3:0] rom_1_data;
  wire [31:0] L_1_84cb7de5_2_out, L_1_84cb7de5_2_oute, L_1_84cb7de5_3_out, L_1_84cb7de5_3_oute,
       L_1_84cb7de5_4_out, L_1_84cb7de5_4_oute, L_1_84cb7de5_out, L_1_84cb7de5_oute;

  and and_1 (and_1_out, rom_1_data[0], CLC);
  and and_2 (and_2_out, rom_1_data[1], CLA);
  and and_3 (and_3_out, rom_1_data[0], CLA);
  and and_4 (and_4_out, rom_1_data[2], CLA);
  and and_5 (and_5_out, rom_1_data[1], CLC);
  and and_6 (and_6_out, rom_1_data[2], CLC);
  and and_7 (and_7_out, LDC, rom_1_data[2]);
  assign BUS_OUT = C ? L_1_84cb7de5_2_out : 32'bz;  // Controlled_Buffer controlled_buffer_1
  and and_8 (and_8_out, LDA, rom_1_data[2]);
  and and_9 (and_9_out, LDA, rom_1_data[1]);
  assign BUS_OUT = A ? L_1_84cb7de5_out : 32'bz;  // Controlled_Buffer controlled_buffer_2
  and and_10 (and_10_out, LDC, rom_1_data[0]);
  and and_11 (and_11_out, LDC, rom_1_data[1]);
  and and_12 (and_12_out, LDA, rom_1_data[0]);
  REG4bcirc_main L_1_84cb7de5 (
    .CLK(CLK), .CLX(and_4_out), .CLXE(and_21_out), .CLH(and_2_out), .CLL(and_3_out), .SIN(and_16_out),
    .LDX(and_8_out), .LDH(and_9_out), .LDL(and_12_out), .IN(BUS_IN), .LDXE(and_22_out),
    .OUT(L_1_84cb7de5_out), .OUTE(L_1_84cb7de5_oute), .SHX(and_13_out), .SHH(and_18_out), .SHL(and_17_out),
    .SHXE(and_26_out));  // open: SOUT
  REG4bcirc_main L_1_84cb7de5_2 (
    .CLK(CLK), .CLX(and_6_out), .CLXE(and_23_out), .CLH(and_5_out), .CLL(and_1_out), .SIN(and_19_out),
    .LDX(and_7_out), .LDH(and_11_out), .LDL(and_10_out), .IN(BUS_IN), .LDXE(and_24_out),
    .OUT(L_1_84cb7de5_2_out), .OUTE(L_1_84cb7de5_2_oute), .SHX(and_14_out), .SHH(and_15_out),
    .SHL(and_20_out), .SHXE(and_25_out));  // open: SOUT
  and and_13 (and_13_out, SHA, rom_1_data[2]);
  assign BUS_OUT = A ? L_1_84cb7de5_oute : 32'bz;  // Controlled_Buffer controlled_buffer_3
  and and_14 (and_14_out, SHC, rom_1_data[2]);
  and and_15 (and_15_out, SHC, rom_1_data[1]);
  assign BUS_OUT = C ? L_1_84cb7de5_2_oute : 32'bz;  // Controlled_Buffer controlled_buffer_4
  and and_16 (and_16_out, SHA, LDA);
  and and_17 (and_17_out, SHA, rom_1_data[0]);
  and and_18 (and_18_out, SHA, rom_1_data[1]);
  and and_19 (and_19_out, SHC, LDC);
  and and_20 (and_20_out, SHC, rom_1_data[0]);
  and and_21 (and_21_out, A, SHA);
  and and_22 (and_22_out, A, LDA);
  and and_23 (and_23_out, C, SHC);
  and and_24 (and_24_out, C, LDC);
  and and_25 (and_25_out, C, CLC);
  ROM #(.addrWidth(4), .dataWidth(4)) rom_1 (.addr({E, X, H, L}), .data(rom_1_data));
  and and_26 (and_26_out, A, CLA);
  and and_27 (and_27_out, rom_1_data[0], CLB);
  and and_28 (and_28_out, rom_1_data[2], CLB);
  and and_29 (and_29_out, rom_1_data[1], CLB);
  assign BUS_OUT = B ? L_1_84cb7de5_3_out : 32'bz;  // Controlled_Buffer controlled_buffer_5
  and and_30 (and_30_out, rom_1_data[2], CLD);
  and and_31 (and_31_out, rom_1_data[1], CLD);
  and and_32 (and_32_out, rom_1_data[0], CLD);
  and and_33 (and_33_out, LDB, rom_1_data[1]);
  and and_34 (and_34_out, LDB, rom_1_data[0]);
  and and_35 (and_35_out, LDB, rom_1_data[2]);
  and and_36 (and_36_out, LDD, rom_1_data[2]);
  and and_37 (and_37_out, LDD, rom_1_data[1]);
  assign BUS_OUT = D ? L_1_84cb7de5_4_out : 32'bz;  // Controlled_Buffer controlled_buffer_6
  REG4bcirc_main L_1_84cb7de5_3 (
    .CLK(CLK), .CLX(and_28_out), .CLXE(and_48_out), .CLH(and_29_out), .CLL(and_27_out), .SIN(and_41_out),
    .LDX(and_35_out), .LDH(and_33_out), .LDL(and_34_out), .IN(BUS_IN), .LDXE(and_47_out),
    .OUT(L_1_84cb7de5_3_out), .OUTE(L_1_84cb7de5_3_oute), .SHX(and_39_out), .SHH(and_42_out),
    .SHL(and_43_out), .SHXE(and_49_out));  // open: SOUT
  and and_38 (and_38_out, LDD, rom_1_data[0]);
  REG4bcirc_main L_1_84cb7de5_4 (
    .CLK(CLK), .CLX(and_30_out), .CLXE(and_51_out), .CLH(and_31_out), .CLL(and_32_out), .SIN(and_44_out),
    .LDX(and_36_out), .LDH(and_37_out), .LDL(and_38_out), .IN(BUS_IN), .LDXE(and_50_out),
    .OUT(L_1_84cb7de5_4_out), .OUTE(L_1_84cb7de5_4_oute), .SHX(and_40_out), .SHH(and_45_out),
    .SHL(and_46_out), .SHXE(and_52_out));  // open: SOUT
  and and_39 (and_39_out, SHB, rom_1_data[2]);
  assign BUS_OUT = B ? L_1_84cb7de5_3_oute : 32'bz;  // Controlled_Buffer controlled_buffer_7
  and and_40 (and_40_out, SHD, rom_1_data[2]);
  assign BUS_OUT = D ? L_1_84cb7de5_4_oute : 32'bz;  // Controlled_Buffer controlled_buffer_8
  and and_41 (and_41_out, SHB, LDB);
  and and_42 (and_42_out, SHB, rom_1_data[1]);
  and and_43 (and_43_out, SHB, rom_1_data[0]);
  and and_44 (and_44_out, SHD, LDD);
  and and_45 (and_45_out, SHD, rom_1_data[1]);
  and and_46 (and_46_out, SHD, rom_1_data[0]);
  and and_47 (and_47_out, B, LDB);
  and and_48 (and_48_out, B, SHB);
  and and_49 (and_49_out, B, CLB);
  and and_50 (and_50_out, D, LDD);
  and and_51 (and_51_out, D, SHD);
  and and_52 (and_52_out, D, CLD);

  // Notes on the sheet:
  //   MOD
  //   contents of rom_1 (hex, n*v repeats v):
  //   1 1 3 3 4*7 4*4 4*8
endmodule
