// Logisim project REG2.circ as structural Verilog: 1 circuit, main circuit main
module main (
  input  SIN,
  input  SHFT,
  input  LOAD,
  input  CLK,
  input  CLR,
  input  [15:0] IN,
  output SOUT,
  output [15:0] OUT
);

  // Shift_Register #(.length(16)) shift_register_1: pin names not known; wires that end beside it: CLR, LOAD, SHFT, CLK, SIN, IN[0], IN[1], IN[2], IN[3], IN[4], IN[5], IN[6], IN[7], IN[8], IN[9], IN[10], IN[11], OUT[0], OUT[1], OUT[2], OUT[3], OUT[4], OUT[5], OUT[6], OUT[7], OUT[8], OUT[9], OUT[10], OUT[11]

  assign SOUT = OUT[15];
endmodule
