// Logisim project REG4.circ as structural Verilog: 1 circuit, main circuit main
module main (
  input  CLK,
  input  SIN,
  input  SHL,
  input  LDL,
  input  CLL,
  input  [7:0] IN,
  output SOUT,
  output [7:0] OUT
);

  // REG1_main L: pin names not known; wires that end beside it: CLL, CLK, SIN, SHL, LDL, SOUT, OUT, IN
endmodule
