// Logisim project REG4bcirc.circ as structural Verilog: 1 circuit, main circuit main
module main (
  input  CLK,
  input  SIN,
  input  LDX,
  input  LDH,
  input  LDL,
  input  [31:0] IN,
  input  SHX,
  input  SHH,
  input  LDXE,
  input  SHL,
  input  SHXE,
  input  CLX,
  input  CLXE,
  input  CLH,
  input  CLL,
  output SOUT,
  output [31:0] OUT,
  output [31:0] OUTE
);

  wire H_p8, L_p8, main_1_p8, shift_register_1_out;

  // REG2_main main_1: pin names not known; wires that end beside it: CLX, OUT[31:16], CLK, SIN, SHX, LDX, IN[31:16], main_1_p8
  // REG1_main H: pin names not known; wires that end beside it: OUT[15:8], CLH, CLK, main_1_p8, SHH, LDH, IN[15:8], H_p8, OUT[7:0]
  // REG1_main L: pin names not known; wires that end beside it: OUT[7:0], CLL, CLK, H_p8, SHL, LDL, IN[7:0], L_p8
  or or_1 (SOUT, L_p8, shift_register_1_out);
  Shift_Register #(.length(32)) shift_register_1 (
    .shift(SHXE), .in(SIN), .clk(CLK), .out(shift_register_1_out), .load(LDXE), .clr(CLXE), .d0(IN[31]),
    .q0(OUTE[31]), .d1(IN[30]), .q1(OUTE[30]), .d2(IN[29]), .q2(OUTE[29]), .d3(IN[28]), .q3(OUTE[28]),
    .d4(IN[27]), .q4(OUTE[27]), .d5(IN[26]), .q5(OUTE[26]), .d6(IN[25]), .q6(OUTE[25]), .d7(IN[24]),
    .q7(OUTE[24]), .d8(IN[23]), .q8(OUTE[23]), .d9(IN[22]), .q9(OUTE[22]), .d10(IN[21]), .q10(OUTE[21]),
    .d11(IN[20]), .q11(OUTE[20]), .d12(IN[19]), .q12(OUTE[19]), .d13(IN[18]), .q13(OUTE[18]), .d14(IN[17]),
    .q14(OUTE[17]), .d15(IN[16]), .q15(OUTE[16]), .d16(IN[15]), .q16(OUTE[15]), .d17(IN[14]), .q17(OUTE[14]),
    .d18(IN[13]), .q18(OUTE[13]), .d19(IN[12]), .q19(OUTE[12]), .d20(IN[11]), .q20(OUTE[11]), .d21(IN[10]),
    .q21(OUTE[10]), .d22(IN[9]), .q22(OUTE[9]), .d23(IN[8]), .q23(OUTE[8]), .d24(IN[7]), .q24(OUTE[7]),
    .d25(IN[6]), .q25(OUTE[6]), .d26(IN[5]), .q26(OUTE[5]), .d27(IN[4]), .q27(OUTE[4]), .d28(IN[3]),
    .q28(OUTE[3]), .d29(IN[2]), .q29(OUTE[2]), .d30(IN[1]), .q30(OUTE[1]), .d31(IN[0]), .q31(OUTE[0]));
endmodule
