// Logisim project REG8.circ as structural Verilog: 1 circuit, main circuit main
module main (
  input  CLK,
  input  SHL,
  input  SIN,
  input  LDL,
  input  CLL,
  input  [7:0] IN,
  input  OP,
  output SOUT,
  output [7:0] OUT
);

  wire [7:0] L_out_8;

  REG1_main L (.CLR(CLL), .CLK(CLK), .SHFT(SHL), .SIN(SIN), .LOAD(LDL), .IN(IN), .SOUT(SOUT), .out_8(L_out_8));
  assign OUT = OP ? L_out_8 : 8'bz;  // Controlled_Buffer controlled_buffer_1
endmodule
