// Logisim project reg8x2.circ as structural Verilog: 1 circuit, main circuit reg8x2
// REGISTERS
module reg8x2 (
  input  CLOCK,
  input  [7:0] BUS_IN,
  input  LOAD_ENABLE,
  input  RESET,
  input  SHIFT,
  input  OUTPUT_ENABLE,
  input  B_REG,
  input  A_REG,
  input  SHIFT_IN,
  input  D_REG,
  input  C_REG,
  output [7:0] BUS_A,
  output [7:0] BUS_B,
  output [7:0] BUS_C,
  output [7:0] BUS_D
);

  wire and_1_out, and_2_out, and_3_out, and_4_out, and_5_out, and_6_out, and_7_out, and_8_out, and_9_out,
       and_10_out, and_11_out, and_12_out, and_13_out, and_14_out, and_15_out, and_16_out,
       REG_SELECTOR_2_p14, REG_SELECTOR_p13;
  wire [7:0] controlled_buffer_1_out, controlled_buffer_2_out, controlled_buffer_3_out,
       controlled_buffer_4_out, controlled_buffer_8_out, controlled_buffer_10_out, REG_SELECTOR_2_p18,
       REG_SELECTOR_p16, shift_register_1_p13, shift_register_2_p16;

  assign controlled_buffer_1_out = LOAD_ENABLE ? BUS_IN : 8'bz;  // Controlled_Buffer controlled_buffer_1
  and and_1 (and_1_out, RESET, A_REG);
  and and_2 (and_2_out, LOAD_ENABLE, A_REG);
  and and_3 (and_3_out, SHIFT, A_REG);
  assign controlled_buffer_2_out = LOAD_ENABLE ? controlled_buffer_1_out : 8'bz;  // Controlled_Buffer controlled_buffer_2
  and and_4 (and_4_out, RESET, C_REG);
  and and_5 (and_5_out, LOAD_ENABLE, C_REG);
  and and_6 (and_6_out, SHIFT, C_REG);
  // Shift_Register REG_SELECTOR: pin names not known; wires that end beside it: controlled_buffer_1_out[6], and_1_out, and_2_out, and_3_out, CLOCK, controlled_buffer_1_out[0], controlled_buffer_1_out[1], controlled_buffer_1_out[2], controlled_buffer_1_out[3], controlled_buffer_1_out[4], controlled_buffer_1_out[5], controlled_buffer_1_out[6], REG_SELECTOR_p13, REG_SELECTOR_p13, REG_SELECTOR_p16[1], REG_SELECTOR_p16[0], REG_SELECTOR_p16[2], REG_SELECTOR_p16[3], REG_SELECTOR_p16[4], REG_SELECTOR_p16[5], REG_SELECTOR_p16[6]
  // Shift_Register REG_SELECTOR_2: pin names not known; wires that end beside it: controlled_buffer_2_out[6], controlled_buffer_1_out[7], and_4_out, and_5_out, and_6_out, controlled_buffer_2_out[0], controlled_buffer_2_out[1], controlled_buffer_2_out[2], controlled_buffer_2_out[3], controlled_buffer_2_out[4], controlled_buffer_2_out[5], controlled_buffer_2_out[6], controlled_buffer_2_out[7], REG_SELECTOR_2_p14, REG_SELECTOR_p16[7], REG_SELECTOR_2_p14, REG_SELECTOR_2_p18[1], REG_SELECTOR_2_p18[0], REG_SELECTOR_2_p18[2], REG_SELECTOR_2_p18[3], REG_SELECTOR_2_p18[4], REG_SELECTOR_2_p18[5], REG_SELECTOR_2_p18[6], REG_SELECTOR_2_p18[7]
  and and_7 (and_7_out, RESET, B_REG);
  and and_8 (and_8_out, LOAD_ENABLE, B_REG);
  and and_9 (and_9_out, SHIFT, B_REG);
  assign controlled_buffer_3_out = A_REG ? REG_SELECTOR_p16 : 8'bz;  // Controlled_Buffer controlled_buffer_3
  assign controlled_buffer_4_out = C_REG ? REG_SELECTOR_2_p18 : 8'bz;  // Controlled_Buffer controlled_buffer_4
  assign BUS_A = and_10_out ? controlled_buffer_3_out : 8'bz;  // Controlled_Buffer controlled_buffer_5
  and and_10 (and_10_out, A_REG, OUTPUT_ENABLE);
  // Shift_Register shift_register_1: pin names not known; wires that end beside it: and_7_out, and_8_out, and_9_out, CLOCK, SHIFT_IN, controlled_buffer_1_out[0], controlled_buffer_1_out[1], controlled_buffer_1_out[2], controlled_buffer_1_out[3], controlled_buffer_1_out[4], controlled_buffer_1_out[5], controlled_buffer_1_out[6], shift_register_1_p13[0], shift_register_1_p13[1], shift_register_1_p13[2], shift_register_1_p13[3], shift_register_1_p13[4], shift_register_1_p13[5], shift_register_1_p13[6]
  and and_11 (and_11_out, RESET, D_REG);
  assign BUS_C = and_14_out ? controlled_buffer_4_out : 8'bz;  // Controlled_Buffer controlled_buffer_6
  and and_12 (and_12_out, LOAD_ENABLE, D_REG);
  and and_13 (and_13_out, SHIFT, D_REG);
  // Shift_Register shift_register_2: pin names not known; wires that end beside it: controlled_buffer_1_out[7], and_11_out, and_12_out, and_13_out, CLOCK, SHIFT_IN, controlled_buffer_2_out[0], controlled_buffer_2_out[1], controlled_buffer_2_out[2], controlled_buffer_2_out[3], controlled_buffer_2_out[4], controlled_buffer_2_out[5], controlled_buffer_2_out[6], controlled_buffer_2_out[7], shift_register_1_p13[7], shift_register_2_p16[0], shift_register_2_p16[1], shift_register_2_p16[2], shift_register_2_p16[3], shift_register_2_p16[4], shift_register_2_p16[5], shift_register_2_p16[6], shift_register_2_p16[7]
  and and_14 (and_14_out, C_REG, OUTPUT_ENABLE);
  assign BUS_B = and_15_out ? controlled_buffer_8_out : 8'bz;  // Controlled_Buffer controlled_buffer_7
  and and_15 (and_15_out, B_REG, OUTPUT_ENABLE);
  assign controlled_buffer_8_out = B_REG ? shift_register_1_p13 : 8'bz;  // Controlled_Buffer controlled_buffer_8
  and and_16 (and_16_out, D_REG, OUTPUT_ENABLE);
  assign BUS_D = and_16_out ? controlled_buffer_10_out : 8'bz;  // Controlled_Buffer controlled_buffer_9
  assign controlled_buffer_10_out = D_REG ? shift_register_2_p16 : 8'bz;  // Controlled_Buffer controlled_buffer_10
endmodule
