// Logisim project regsel.circ as structural Verilog: 1 circuit, main circuit main
module main (
  input  r0,
  input  r1,
  input  r2,
  input  r3,
  output [3:0] out_5
);

  ROM #(.addrWidth(4), .dataWidth(4)) rom_1 (.addr({r3, r2, r1, r0}), .data(out_5), .sel(1'b1));

  // Notes on the sheet:
  //   contents of rom_1 (hex, n*v repeats v):
  //   0 1 2 3 4 5 6 7 8 9 a b c d e f
endmodule
