// Logisim project small_counter.circ as structural Verilog: 1 circuit, main circuit main
module main (
  input  [7:0] BUS_IN,
  input  INS_INC,
  input  CLK,
  input  JMP,
  output [7:0] BUS_OUT
);

  Clock clock_1 ();  // open: out
  Register register_1 (.D(BUS_IN), .en(INS_INC), .clk(CLK), .Q(BUS_OUT), .clr(JMP));
endmodule
