// Logisim project transceiver.circ as structural Verilog: 1 circuit, main circuit main
module main (
  input  [7:0] BIN0,
  input  [7:0] BIN1,
  input  AC,
  input  BC,
  input  ALU_O,
  output [7:0] BOUT
);

  wire and_1_out, and_2_out, not_1_out, not_2_out, not_3_out;
  wire [7:0] controlled_buffer_1_out;

  not not_1 (not_1_out, BC);
  not not_2 (not_2_out, AC);
  assign controlled_buffer_1_out = and_2_out ? BIN1 : 8'bz;  // Controlled_Buffer controlled_buffer_1
  and and_1 (and_1_out, AC, not_1_out);
  and and_2 (and_2_out, not_2_out, BC);
  not not_3 (not_3_out, ALU_O);
  assign controlled_buffer_1_out = and_1_out ? BIN0 : 8'bz;  // Controlled_Buffer controlled_buffer_2
  assign BOUT = not_3_out ? controlled_buffer_1_out : 8'bz;  // Controlled_Buffer controlled_buffer_3
endmodule
