// Logisim project ALU.circ as structural Verilog: 1 circuit, main circuit ALU
module ALU (
  input  [7:0] BUS_IN_A,
  input  [7:0] BUS_IN_B,
  input  ANDOR,
  input  DIVIDE,
  input  SUBSTRACT,
  input  E0,
  output PARITY,
  output BORROW,
  output ZERO,
  output CARRY,
  output LT,
  output EQ,
  output GT,
  output [7:0] BUS_OUT
);

  wire or_2_out;
  wire [7:0] adder_1_out, and_1_out, divider_1_out, multiplexer_1_out, multiplier_1_out, negator_1_out,
       or_1_out, subtractor_1_out;
  wire [31:0] fpadder_1_out, fptoint_2_p2, register_1_q, register_2_q, register_3_q, shifter_1_out,
       shifter_2_out, shifter_3_out;

  Shifter #(.width(32)) shifter_1 (.in({{24{1'b0}}, BUS_IN_A}), .\dist (5'b01000), .out(shifter_1_out));
  Shifter #(.width(32)) shifter_2 (.in({{24{1'b0}}, BUS_IN_B}), .\dist (5'b01000), .out(shifter_2_out));
  Register #(.width(32)) register_1 (.D(shifter_1_out), .en(E0), .clk(E0), .Q(register_1_q), .clr(1'b0));
  Register #(.width(32)) register_2 (.D(shifter_2_out), .en(E0), .clk(E0), .Q(register_2_q), .clr(1'b0));
  assign and_1_out = BUS_IN_A & BUS_IN_B;  // AND_Gate and_1, 8 bits wide
  assign or_1_out = BUS_IN_A | BUS_IN_B;  // OR_Gate or_1, 8 bits wide
  FPAdder fpadder_1 (.a(register_1_q), .b(register_2_q), .out(fpadder_1_out));
  FPSubtractor fpsubtractor_1 ();  // open: a, b, out
  FPMultiplier fpmultiplier_1 ();  // open: a, b, out
  FPDivider fpdivider_1 ();  // open: a, b, out
  // FPNegator fpnegator_1: pin names not known
  // FPComparator fpcomparator_1: pin names not known
  // FPToInt fptoint_1: pin names not known
  // IntToFP inttofp_1: pin names not known
  Adder adder_1 (.a(BUS_IN_A), .b(BUS_IN_B), .out(adder_1_out), .cin(SUBSTRACT), .cout(CARRY));
  Subtractor subtractor_1 (.a(BUS_IN_A), .b(BUS_IN_B), .out(subtractor_1_out), .bout(BORROW));  // open: bin
  Multiplier multiplier_1 (.a(BUS_IN_A), .b(BUS_IN_B), .out(multiplier_1_out));  // open: cin, cout
  Divider divider_1 (.a(BUS_IN_A), .b(BUS_IN_B), .out(divider_1_out));  // open: upper, rem
  Comparator comparator_1 (.a(BUS_IN_A), .b(BUS_IN_B), .gt(LT), .eq(EQ), .lt(GT));
  Negator negator_1 (.in(BUS_IN_A), .out(negator_1_out));
  Divider divider_2 ();  // open: a, b, out, upper, rem
  Negator negator_2 ();  // open: in, out
  Comparator comparator_2 ();  // open: a, b, gt, eq, lt
  Multiplexer #(.enable("true"), .select(3), .width(8)) multiplexer_1 (
    .in0(adder_1_out), .in1(subtractor_1_out), .in2(multiplier_1_out), .in3(divider_1_out),
    .in4(negator_1_out), .in5(and_1_out), .in6(or_1_out), .out(multiplexer_1_out),
    .sel({ANDOR, DIVIDE, SUBSTRACT}), .en(E0));  // open: in7
  // FPToInt #(.width(32)) fptoint_2: pin names not known; wires that end beside it: fpadder_1_out, fptoint_2_p2
  Register #(.width(32)) register_3 (.D(fptoint_2_p2), .en(E0), .clk(E0), .Q(register_3_q), .clr(1'b0));
  assign BUS_OUT = or_2_out ? multiplexer_1_out : 8'bz;  // Controlled_Buffer controlled_buffer_1
  or or_2 (or_2_out, SUBSTRACT, E0);
  nor nor_1 (ZERO, multiplexer_1_out[0], multiplexer_1_out[1], multiplexer_1_out[2], multiplexer_1_out[3], multiplexer_1_out[4], multiplexer_1_out[5], multiplexer_1_out[6], multiplexer_1_out[7]);
  not not_1 (PARITY, multiplexer_1_out[0]);
  Shifter #(.shift("lr"), .width(32)) shifter_3 (.in(register_3_q), .\dist (5'b01000), .out(shifter_3_out));
endmodule
