// Logisim project Instruction_Register.circ as structural Verilog: 1 circuit, main circuit IR
module IR (
  input  CLK,
  input  INSI,
  input  [7:0] FWI,
  output [7:0] FWO
);

  Register register_1 (.D(FWI), .en(INSI), .Q(FWO), .clk(CLK), .clr(1'b0));
endmodule
