// Logisim project Memory_Addres_Register.circ as structural Verilog: 1 circuit, main circuit MAR
module MAR (
  input  CLK,
  input  MI,
  input  [7:0] BIN1,
  input  [7:0] BIN2,
  input  [7:0] BIN3,
  input  [7:0] BIN4,
  output [7:0] out_7,
  output [7:0] out_8,
  output [7:0] out_9,
  output [7:0] out_10
);

  Register register_1 (.D(BIN1), .en(MI), .Q(out_7), .clk(CLK), .clr(1'b0));
  Register register_2 (.D(BIN2), .en(MI), .Q(out_8), .clk(CLK), .clr(1'b0));
  Register register_3 (.D(BIN3), .en(MI), .Q(out_9), .clk(CLK), .clr(1'b0));
  Register register_4 (.D(BIN4), .en(MI), .Q(out_10), .clk(CLK), .clr(1'b0));
endmodule
