// Logisim project Program_Counter.circ as structural Verilog: 1 circuit, main circuit Program_Counter
module Program_Counter (
  input  CLK,
  input  SHIN,
  input  CE,
  input  JMP,
  input  RST,
  input  CO,
  input  SHOUT,
  input  [7:0] BIN1,
  output [7:0] BOUT1,
  output [7:0] BOUT2,
  output [7:0] BOUT3,
  output [7:0] BOUT4,
  output [7:0] BOUTS,
  output ERR
);

  wire [7:0] shift_register_1_out, shift_register_1_q0, shift_register_1_q1, shift_register_1_q2,
       shift_register_2_out;
  wire [31:0] counter_1_q;

  Shift_Register #(.length(4), .width(8)) shift_register_1 (
    .shift(SHIN), .in(BIN1), .clk(CLK), .out(shift_register_1_out), .load(1'b0), .clr(1'b0),
    .q0(shift_register_1_q0), .q1(shift_register_1_q1), .q2(shift_register_1_q2));  // open: d0, d1, d2, d3, q3
  Counter #(.max('hffffffff), .width(32)) counter_1 (
    .load(JMP), .D({shift_register_1_q0, shift_register_1_q1, shift_register_1_q2, shift_register_1_out}),
    .count(CE), .Q(counter_1_q), .carry(ERR), .up(1'b1), .clk(CLK), .clr(RST));
  assign {BOUT4, BOUT3, BOUT2, BOUT1} = CO ? counter_1_q : 32'bz;  // Controlled_Buffer controlled_buffer_1
  Shift_Register #(.length(4), .width(8)) shift_register_2 (
    .shift(SHOUT), .clk(CLK), .out(shift_register_2_out), .load(CO), .clr(1'b0), .d0(BOUT4), .d1(BOUT3),
    .d2(BOUT2), .d3(BOUT1));  // open: in, q0, q1, q2, q3
  assign BOUTS = SHOUT ? shift_register_2_out : 8'bz;  // Controlled_Buffer controlled_buffer_2
endmodule
