// Logisim project STACK.circ as structural Verilog: 1 circuit, main circuit STACK
module STACK (
  input  [7:0] COUNTER_IN,
  input  CPP,
  input  CMM,
  input  CLK,
  input  [7:0] DATA,
  input  LRS,
  input  LR2,
  input  LR0,
  input  LRW,
  output [7:0] BUSO
);

  wire and_1_out, and_2_out, and_3_out, and_4_out, and_5_out, and_6_out, and_7_out, and_8_out, and_9_out,
       and_10_out, and_11_out, and_12_out, and_13_out, decoder_1_out1, decoder_1_out2, decoder_1_out3,
       decoder_2_out1, decoder_2_out2, decoder_2_out3, decoder_2_out5, decoder_2_out6, decoder_2_out7,
       multiplexer_1_out, not_1_out, or_1_out, or_2_out, or_3_out, or_4_out, or_5_out, or_6_out, or_7_out,
       or_8_out, or_9_out, or_10_out;
  wire [7:0] controlled_buffer_1_out, controlled_buffer_2_out, controlled_buffer_3_out,
       controlled_buffer_4_out, counter_1_q, counter_2_q, multiplexer_2_out, ram_1_dout, ram_2_dout,
       ram_3_dout;

  not not_1 (not_1_out, LRS);
  Decoder #(.select(2)) decoder_1 (
    .out1(decoder_1_out1), .out2(decoder_1_out2), .out3(decoder_1_out3), .sel({CPP, CMM}), .en(1'b1));  // open: out0
  Multiplexer #(.enable("false")) multiplexer_1 (
    .in0(decoder_1_out1), .in1(decoder_1_out2), .out(multiplexer_1_out), .sel(decoder_1_out2));
  and and_1 (and_1_out, decoder_1_out3, LRS);
  and and_2 (and_2_out, decoder_1_out2, LRS);
  and and_3 (and_3_out, decoder_1_out1, LRS);
  and and_4 (and_4_out, not_1_out, multiplexer_1_out);
  Counter counter_1 (
    .load(and_1_out), .D(COUNTER_IN), .count(or_1_out), .Q(counter_1_q), .up(and_2_out), .clk(CLK), .clr(1'b0));  // open: carry
  or or_1 (or_1_out, and_2_out, and_3_out);
  Counter counter_2 (
    .load(1'b0), .D(COUNTER_IN), .count(and_4_out), .Q(counter_2_q), .up(decoder_1_out2), .clk(CLK),
    .clr(1'b0));  // open: carry
  Decoder #(.select(3)) decoder_2 (
    .out1(decoder_2_out1), .out2(decoder_2_out2), .out3(decoder_2_out3), .out5(decoder_2_out5),
    .out6(decoder_2_out6), .out7(decoder_2_out7), .sel({LRW, LR2, LR0}));  // open: out0, out4, en
  Multiplexer #(.enable("false"), .width(8)) multiplexer_2 (
    .in0(counter_2_q), .in1(counter_1_q), .out(multiplexer_2_out), .sel(LRS));
  RAM #(.asyncread("true")) ram_1 (
    .addr(multiplexer_2_out), .we(or_2_out), .oe(and_7_out), .clk(CLK), .din(DATA), .dout(ram_1_dout));
  or or_2 (or_2_out, and_5_out, and_6_out);
  and and_5 (and_5_out, LRW, decoder_2_out3);
  and and_6 (and_6_out, LRW, decoder_2_out7);
  assign controlled_buffer_1_out = and_7_out ? ram_1_dout : 8'bz;  // Controlled_Buffer controlled_buffer_1
  and and_7 (and_7_out, ~LRW, or_4_out);  // AND_Gate
  or or_3 (or_3_out, and_8_out, and_9_out);
  or or_4 (or_4_out, decoder_2_out3, decoder_2_out7);
  and and_8 (and_8_out, LRW, decoder_2_out2);
  RAM #(.asyncread("true")) ram_2 (
    .addr(multiplexer_2_out), .we(or_3_out), .oe(and_10_out), .clk(CLK), .din(DATA), .dout(ram_2_dout));
  and and_9 (and_9_out, LRW, decoder_2_out6);
  and and_10 (and_10_out, ~LRW, or_5_out);  // AND_Gate
  or or_5 (or_5_out, decoder_2_out2, decoder_2_out6);
  and and_11 (and_11_out, LRW, decoder_2_out1);
  assign controlled_buffer_2_out = and_10_out ? ram_2_dout : 8'bz;  // Controlled_Buffer controlled_buffer_2
  or or_6 (or_6_out, and_11_out, and_12_out);
  and and_12 (and_12_out, LRW, decoder_2_out5);
  and and_13 (and_13_out, ~LRW, or_10_out);  // AND_Gate
  or or_7 (or_7_out, decoder_2_out1, decoder_2_out2, decoder_2_out3);
  or or_8 (or_8_out, or_7_out, or_9_out);
  or or_9 (or_9_out, decoder_2_out5, decoder_2_out6, decoder_2_out7);
  RAM #(.asyncread("true")) ram_3 (
    .addr(multiplexer_2_out), .we(or_6_out), .oe(and_13_out), .clk(CLK), .din(DATA), .dout(ram_3_dout));
  assign controlled_buffer_3_out = and_13_out ? ram_3_dout : 8'bz;  // Controlled_Buffer controlled_buffer_3
  assign controlled_buffer_4_out = or_8_out ? multiplexer_2_out : 8'bz;  // Controlled_Buffer controlled_buffer_4
  or or_10 (or_10_out, decoder_2_out1, decoder_2_out5);
  Multiplexer #(.enable("false"), .select(2), .width(8)) multiplexer_3 (
    .in0(controlled_buffer_4_out), .in1(controlled_buffer_3_out), .in2(controlled_buffer_2_out),
    .in3(controlled_buffer_1_out), .out(BUSO), .sel({LR2, LR0}));
endmodule
