// Logisim project transceiver.circ as structural Verilog: 1 circuit, main circuit MUX
module MUX (
  input  [7:0] BIN0,
  input  [7:0] BIN1,
  input  [7:0] BIN2,
  input  [7:0] BIN3,
  input  ALU_O,
  input  DC,
  input  CC,
  input  BC,
  input  AC,
  output [7:0] BOUT
);

  wire or_1_out;
  wire [7:0] multiplexer_1_out;

  Multiplexer #(.disabled("Z"), .enable("true"), .select(4), .width(8)) multiplexer_1 (
    .in1(BIN0), .in2(BIN1), .in3(BIN0), .in4(BIN2), .in5(BIN0), .in8(BIN3), .in9(BIN0),
    .out(multiplexer_1_out), .sel({DC, CC, BC, AC}), .en(or_1_out));  // open: in0, in6, in7, in10, in11, in12, in13, in14, in15
  or or_1 (or_1_out, DC, CC, BC, AC);
  assign BOUT = or_1_out ? multiplexer_1_out : 8'bz;  // Controlled_Buffer controlled_buffer_1
endmodule
