// Logisim project MAR.circ as structural Verilog: 1 circuit, main circuit main
module main (
  input  JMP,
  input  CLK,
  input  [7:0] BUS_IN,
  input  CO,
  output [7:0] BUS_OUT
);

  wire decoder_1_out15, not_1_out, or_1_out;
  wire [7:0] counter_1_q;

  Counter counter_1 (
    .clr(or_1_out), .load(JMP), .up(not_1_out), .count(not_1_out), .clk(CLK), .D(BUS_IN), .Q(counter_1_q));  // open: carry
  or or_1 (or_1_out, decoder_1_out15, 1'b0);
  not not_1 (not_1_out, 1'b0);
  Decoder #(.select(4)) decoder_1 (
    .out15(decoder_1_out15), .sel(counter_1_q[3:0]), .en(not_1_out));  // open: out0, out1, out2, out3, out4, out5, out6, out7, out8, out9, out10, out11, out12, out13, out14
  assign BUS_OUT = CO ? counter_1_q : 8'bz;  // Controlled_Buffer controlled_buffer_1
endmodule
