// Logisim project PC.circ as structural Verilog: 1 circuit, main circuit main
module main (
  input  IN1,
  input  PCCLR,
  input  CLK,
  input  [7:0] BUS_IN,
  output [7:0] BUS_OUT
);

  wire d_ff_1_q, d_ff_2_q, nand_1_out, not_1_out, not_2_out, undriven;

  D_Flip_Flop #(.trigger("high")) d_ff_1 (.clk(CLK), .D(IN1), .Q(d_ff_1_q), .en(CLK));  // open: Qn, preset, reset
  // OR_Gate or_1 is placed but not wired
  not not_1 (not_1_out, CLK);
  Counter counter_1 (.load(1'b0), .D(BUS_IN), .count(CLK), .Q(BUS_OUT), .clk(CLK), .clr(d_ff_2_q));  // open: carry
  not not_2 (not_2_out, PCCLR);
  D_Flip_Flop #(.trigger("high")) d_ff_2 (
    .clk(not_1_out), .D(PCCLR), .Q(d_ff_2_q), .preset(1'b0), .en(PCCLR), .reset(not_2_out));  // open: Qn
  Controlled_Buffer controlled_buffer_1 (.in(nand_1_out), .en(undriven));  // open: out
  nand nand_1 (nand_1_out, BUS_OUT[4], BUS_OUT[7], BUS_OUT[6], BUS_OUT[5], BUS_OUT[3], BUS_OUT[2], BUS_OUT[1], BUS_OUT[0]);
endmodule
