// Logisim project MAR.circ as structural Verilog: 1 circuit, main circuit main
module main (
  input  [7:0] IN2,
  input  [7:0] IN1,
  input  [7:0] IN0,
  input  MI2,
  input  MI0,
  input  MII,
  input  CLK,
  output [7:0] RAM2,
  output [7:0] RAM1,
  output [7:0] RAM0
);

  wire decoder_1_out0, decoder_1_out1, decoder_1_out2, decoder_1_out3, or_1_out, or_2_out, or_3_out,
       or_4_out, or_5_out, or_6_out;
  wire [7:0] controlled_buffer_1_out, controlled_buffer_2_out, controlled_buffer_3_out;

  Decoder #(.select(2)) decoder_1 (
    .out0(decoder_1_out0), .out1(decoder_1_out1), .out2(decoder_1_out2), .out3(decoder_1_out3),
    .sel({MI2, MI0}), .en(1'b1));
  assign controlled_buffer_1_out = or_2_out ? IN1 : 8'bz;  // Controlled_Buffer controlled_buffer_1
  assign controlled_buffer_2_out = or_1_out ? IN0 : 8'bz;  // Controlled_Buffer controlled_buffer_2
  or or_1 (or_1_out, MII, decoder_1_out1);
  or or_2 (or_2_out, MII, decoder_1_out2);
  assign controlled_buffer_3_out = or_3_out ? IN2 : 8'bz;  // Controlled_Buffer controlled_buffer_3
  or or_3 (or_3_out, MII, decoder_1_out3);
  or or_4 (or_4_out, decoder_1_out1, MII);
  or or_5 (or_5_out, decoder_1_out3, MII);
  or or_6 (or_6_out, decoder_1_out2, MII);
  Register #(.trigger("high")) register_1 (.D(controlled_buffer_3_out), .en(or_5_out), .Q(RAM2), .clk(CLK), .clr(1'b0));
  Register #(.trigger("high")) register_2 (.D(controlled_buffer_1_out), .en(or_6_out), .Q(RAM1), .clk(CLK), .clr(1'b0));
  Register #(.trigger("high")) register_3 (.D(controlled_buffer_2_out), .en(or_4_out), .Q(RAM0), .clk(CLK), .clr(1'b0));
endmodule
