// Logisim project STACK.circ as structural Verilog: 1 circuit, main circuit main
// STACK
module main (
  input  [7:0] COUNTER_IN,
  input  C_plus_plus,
  input  C_minus_minus,
  input  CLK,
  input  [7:0] DATA,
  input  LRO,
  input  LR2,
  input  LR0,
  output [7:0] out_9,
  output [7:0] out_10,
  output [7:0] out_11
);

  wire and_1_out, and_2_out, and_3_out, and_4_out, and_5_out, and_6_out, decoder_1_out1, decoder_1_out2,
       decoder_1_out3, or_1_out, or_2_out, or_3_out, or_4_out;
  wire [7:0] counter_1_q, ram_1_data, ram_2_data, ram_3_data;

  or or_1 (or_1_out, C_plus_plus, C_minus_minus);
  Counter counter_1 (
    .load(C_minus_minus), .D(COUNTER_IN), .count(or_1_out), .Q(counter_1_q), .clk(CLK));  // open: carry, clr
  and and_1 (and_1_out, LRO, decoder_1_out3);
  and and_2 (and_2_out, decoder_1_out1, ~LRO);  // AND_Gate
  and and_3 (and_3_out, LRO, decoder_1_out2);
  and and_4 (and_4_out, LRO, decoder_1_out1);
  RAM #(.bus("separate")) ram_1 (
    .addr(counter_1_q), .din(DATA), .data(ram_1_data), .str(and_2_out), .sel(or_2_out), .clk(CLK),
    .ld(or_2_out));  // open: clr
  or or_2 (or_2_out, and_4_out, decoder_1_out1);
  Decoder #(.select(2)) decoder_1 (
    .out1(decoder_1_out1), .out2(decoder_1_out2), .out3(decoder_1_out3), .sel({LR2, LR0}), .en(1'b1));  // open: out0
  assign out_11 = or_2_out ? ram_1_data : 8'bz;  // Controlled_Buffer controlled_buffer_1
  and and_5 (and_5_out, decoder_1_out2, ~LRO);  // AND_Gate
  RAM #(.bus("separate")) ram_2 (
    .addr(counter_1_q), .din(DATA), .data(ram_2_data), .str(and_5_out), .sel(or_3_out), .clk(CLK),
    .ld(or_3_out), .clr(1'b0));
  or or_3 (or_3_out, and_3_out, decoder_1_out2);
  assign out_10 = or_3_out ? ram_2_data : 8'bz;  // Controlled_Buffer controlled_buffer_2
  and and_6 (and_6_out, decoder_1_out3, ~LRO);  // AND_Gate
  RAM #(.bus("separate")) ram_3 (
    .addr(counter_1_q), .din(DATA), .data(ram_3_data), .str(and_6_out), .sel(or_4_out), .clk(CLK),
    .ld(or_4_out), .clr(1'b0));
  or or_4 (or_4_out, and_1_out, decoder_1_out3);
  assign out_9 = or_4_out ? ram_3_data : 8'bz;  // Controlled_Buffer controlled_buffer_3
endmodule
