// Logisim project PC_IR_MAR.circ as structural Verilog: 1 circuit, main circuit main
module main (
  input  LRO,
  input  LR2,
  input  LR0,
  input  [7:0] B_IN,
  input  [7:0] in_5,
  input  CLK,
  input  II,
  input  IRC,
  input  CE,
  input  J2,
  input  J0,
  input  CO,
  input  MI2,
  input  MI0,
  output [7:0] B_OUT,
  output [7:0] IR_OUT,
  output [7:0] MAR0,
  output [7:0] MAR1,
  output [7:0] MAR2
);

  wire and_1_out, and_2_out, and_3_out, and_4_out, and_5_out, and_6_out, and_9_out, and_10_out, and_11_out,
       and_12_out, CC_2_carry, CC_3_carry, controlled_buffer_1_out, controlled_buffer_2_out,
       controlled_buffer_3_out, decoder_1_out1, decoder_1_out2, decoder_1_out3, decoder_1_out4,
       decoder_1_out5, decoder_1_out6, decoder_1_out7, decoder_2_out1, decoder_2_out2, decoder_2_out3,
       decoder_3_out0, decoder_3_out1, decoder_3_out2, decoder_3_out3, decoder_4_out0, decoder_4_out1,
       decoder_4_out2, decoder_4_out3, not_1_out, not_2_out, not_3_out, or_1_out, or_2_out, or_3_out,
       or_4_out, or_5_out, or_6_out, or_7_out, or_9_out, or_10_out, or_11_out;
  wire [7:0] CC_2_q, CC_3_q, CC_q, controlled_buffer_8_out, controlled_buffer_9_out,
       controlled_buffer_10_out, controlled_buffer_11_out, controlled_buffer_12_out,
       controlled_buffer_16_out, counter_1_q, ram_1_data, ram_2_data, ram_3_data;

  Decoder #(.select(3)) decoder_1 (
    .out1(decoder_1_out1), .out2(decoder_1_out2), .out3(decoder_1_out3), .out4(decoder_1_out4),
    .out5(decoder_1_out5), .out6(decoder_1_out6), .out7(decoder_1_out7), .sel({LRO, LR2, LR0}), .en(1'b1));  // open: out0
  assign controlled_buffer_1_out = not_1_out ? and_4_out : 1'bz;  // Controlled_Buffer controlled_buffer_1
  assign controlled_buffer_2_out = not_1_out ? and_3_out : 1'bz;  // Controlled_Buffer controlled_buffer_2
  assign controlled_buffer_3_out = not_1_out ? and_5_out : 1'bz;  // Controlled_Buffer controlled_buffer_3
  not not_1 (not_1_out, CO);
  or or_1 (or_1_out, decoder_1_out5, decoder_1_out6);
  and and_1 (and_1_out, CE, CC_2_carry);
  and and_2 (and_2_out, CE, CC_3_carry);
  and and_3 (and_3_out, decoder_2_out1, or_2_out);
  Decoder #(.select(2)) decoder_2 (
    .out1(decoder_2_out1), .out2(decoder_2_out2), .out3(decoder_2_out3), .sel({J2, J0}), .en(1'b1));  // open: out0
  Counter counter_1 (
    .load(decoder_1_out6), .D(B_IN), .count(or_1_out), .Q(counter_1_q), .clk(CLK), .clr(decoder_1_out7));  // open: carry
  assign B_OUT = not_1_out ? in_5 : 8'bz;  // Controlled_Buffer controlled_buffer_4
  assign B_OUT = or_4_out ? CC_q : 8'bz;  // Controlled_Buffer controlled_buffer_5
  Counter CC (
    .load(controlled_buffer_3_out), .D(B_IN), .count(and_1_out), .Q(CC_q), .clk(CLK), .clr(1'b0));  // open: carry
  assign B_OUT = or_5_out ? CC_2_q : 8'bz;  // Controlled_Buffer controlled_buffer_6
  Counter CC_2 (
    .load(controlled_buffer_1_out), .D(B_IN), .count(and_2_out), .Q(CC_2_q), .carry(CC_2_carry), .clk(CLK),
    .clr(1'b0));
  assign B_OUT = or_3_out ? CC_3_q : 8'bz;  // Controlled_Buffer controlled_buffer_7
  Counter CC_3 (
    .load(controlled_buffer_2_out), .D(B_IN), .count(CE), .Q(CC_3_q), .carry(CC_3_carry), .clk(CLK),
    .clr(1'b0));
  and and_4 (and_4_out, decoder_2_out2, or_2_out);
  and and_5 (and_5_out, decoder_2_out3, or_2_out);
  or or_2 (or_2_out, J2, J0);
  or or_3 (or_3_out, and_6_out, decoder_3_out1);
  and and_6 (and_6_out, CO, decoder_3_out0);
  Decoder #(.select(2)) decoder_3 (
    .out0(decoder_3_out0), .out1(decoder_3_out1), .out2(decoder_3_out2), .out3(decoder_3_out3),
    .sel({J2, J0}), .en(1'b1));
  RAM #(.bus("separate")) ram_1 (
    .addr(counter_1_q), .din(B_IN), .data(ram_1_data), .str(decoder_1_out3), .sel(1'b1), .clk(CLK),
    .ld(decoder_1_out1));  // open: clr
  or or_4 (or_4_out, and_6_out, decoder_3_out3);
  or or_5 (or_5_out, and_6_out, decoder_3_out2);
  assign controlled_buffer_8_out = decoder_1_out4 ? ram_1_data : 8'bz;  // Controlled_Buffer controlled_buffer_8
  assign controlled_buffer_9_out = or_6_out ? B_OUT : 8'bz;  // Controlled_Buffer controlled_buffer_9
  assign controlled_buffer_10_out = or_6_out ? B_OUT : 8'bz;  // Controlled_Buffer controlled_buffer_10
  // AND_Gate and_7 has open pins: in0=or_6_out, out=open
  assign controlled_buffer_11_out = or_6_out ? B_OUT : 8'bz;  // Controlled_Buffer controlled_buffer_11
  or or_6 (or_6_out, CO, or_7_out);
  RAM #(.bus("separate")) ram_2 (
    .addr(counter_1_q), .din(B_IN), .data(ram_2_data), .str(decoder_1_out2), .sel(1'b1), .clk(CLK),
    .ld(decoder_1_out2), .clr(1'b0));
  not not_2 (not_2_out, or_7_out);
  // AND_Gate and_8 has open pins: in0=or_6_out, out=open
  or or_7 (or_7_out, MI2, MI0);
  assign controlled_buffer_12_out = decoder_1_out4 ? ram_2_data : 8'bz;  // Controlled_Buffer controlled_buffer_12
  assign controlled_buffer_11_out = or_7_out ? B_OUT : 8'bz;  // Controlled_Buffer controlled_buffer_13
  Register register_1 (.D(B_IN), .en(II), .Q(IR_OUT), .clk(CLK), .clr(IRC));
  RAM #(.bus("separate")) ram_3 (
    .addr(counter_1_q), .din(B_IN), .data(ram_3_data), .str(decoder_1_out1), .sel(1'b1), .clk(CLK),
    .ld(decoder_1_out3), .clr(1'b0));
  assign controlled_buffer_10_out = or_7_out ? B_OUT : 8'bz;  // Controlled_Buffer controlled_buffer_14
  assign controlled_buffer_9_out = or_7_out ? B_OUT : 8'bz;  // Controlled_Buffer controlled_buffer_15
  and and_9 (and_9_out, decoder_4_out0, CO);
  and and_10 (and_10_out, decoder_4_out0, CO);
  Decoder #(.select(2)) decoder_4 (
    .out0(decoder_4_out0), .out1(decoder_4_out1), .out2(decoder_4_out2), .out3(decoder_4_out3),
    .sel({MI2, MI0}), .en(1'b1));
  assign controlled_buffer_16_out = decoder_1_out4 ? ram_3_data : 8'bz;  // Controlled_Buffer controlled_buffer_16
  and and_11 (and_11_out, not_2_out, decoder_1_out4);
  not not_3 (not_3_out, and_11_out);
  assign controlled_buffer_16_out = not_3_out ? controlled_buffer_9_out : 8'bz;  // Controlled_Buffer controlled_buffer_17
  assign controlled_buffer_12_out = not_3_out ? controlled_buffer_10_out : 8'bz;  // Controlled_Buffer controlled_buffer_18
  assign controlled_buffer_8_out = not_3_out ? controlled_buffer_11_out : 8'bz;  // Controlled_Buffer controlled_buffer_19
  and and_12 (and_12_out, decoder_4_out0, CO);
  // OR_Gate or_8 has open pins: in0=MI2, in1=MI0, out=open
  or or_9 (or_9_out, and_10_out, decoder_4_out1);
  or or_10 (or_10_out, and_9_out, decoder_4_out2);
  or or_11 (or_11_out, and_12_out, decoder_4_out3);
  Register register_2 (.D(controlled_buffer_16_out), .en(or_9_out), .Q(MAR0), .clk(CLK), .clr(1'b0));
  Register register_3 (.D(controlled_buffer_12_out), .en(or_10_out), .Q(MAR1), .clk(CLK), .clr(1'b0));
  Register register_4 (.D(controlled_buffer_8_out), .en(or_11_out), .Q(MAR2), .clk(CLK), .clr(1'b0));
endmodule
