// Logisim project UC.circ as structural Verilog: 1 circuit, main circuit CONTROL_UNIT
module CONTROL_UNIT (
  input  [7:0] PC_IN,
  input  [7:0] IR_IN,
  input  CLK,
  output [15:0] PC_OUT
);

  wire [7:0] register_1_q, register_2_q;
  wire [15:8] undriven;

  Register register_1 (.D(PC_IN), .en(1'b1), .clk(CLK), .Q(register_1_q), .clr(1'b0));
  Register register_2 (.D(IR_IN), .en(1'b1), .clk(CLK), .Q(register_2_q), .clr(1'b0));
  ROM #(.addrWidth(16), .dataWidth(16)) FIRMWARE (.addr({undriven, register_1_q}), .data(PC_OUT));

  // Notes on the sheet:
  //   contents of FIRMWARE (hex, n*v repeats v):
  //   60 a800 60 4b 8020 8008 27 60 60 a800 60 a800 60 a800 60 a800 60 a800 60 4b 8020 8009 27 60 60 a800
  //   60 a800 60 a800 60 a800 60 a800 60 4b 8020 8009 205 27 60 60 a800 a800 60 a800 60 a800 60 a800 60 4b
  //   8020 8009 305 27 60 60 a800 a800 60 a800 60 a800 60 a800 2004 60 a800 a800 60 a800 60 a800 60 a800
  //   60 a800 60 a800 60 a800 60 a800 60 a800 60 a800 60 a800 60 a800 60 a800 60 a800 60 a800 60 a800 60
  //   a800 60 a800 60 a800 60 a800 60 a800 60 a800 60 a800 60 a800 60 a800 60 a800 60 a800 60 a800 60 a800
  //   60 a800 60 a800 60 a800 60 a800 60 a800 60 a800 60 a800 60 a800 60 a800 60 a800 60 a800 60 a800 60
  //   a800 60 a800 60 a800 60 a800 60 a800 60 a800 60 a800 60 a800 60 a800 60 a800 60 a800 60 a800 60 a800
  //   60 a800 60 a800 60 a800 60 a800 60 a800 60 a800 60 a800 60 a800 60 a800 60 a800 60 a800 60 a800 60
  //   a800 60 a800 60 a800 60 a800 60 a800 60 a800 60 a800 60 a800 60 a800 60 a800 60 a800 60 a800 60 a800
  //   60 a800 60 a800 60 a800 60 a800 60 a800 60 a800 60 a800 60 a800 60 a800 60 a800 60 a800 60 a800 60
  //   a800 60 a800 60 a800
endmodule
