// Logisim project libre8.circ as structural Verilog: 1 circuit, main circuit Libre 8
module Libre_8 (
  input  PULSE
);

  wire ALU_EOUT, ALU_SUB, and_1_out, and_2_out, CE, CMM, CO, COUT, CPP, FI, HALT, IR_IN, IR_OUT, J0, J2, KBI,
       KBO, keyboard_1_avail, LR0, LR2, LRO, main_1_clk, main_1_nclk, main_4_out_10, main_4_out_11, MI0, MI2,
       MII, or_1_out, or_2_out, PCCLR, r0, r1, r2, r3, RAM_IN, RAM_OUT;
  wire [1:0] register_2_q, simple_alu_1_p5;
  wire [3:0] controlled_buffer_1_out, controlled_buffer_1_out_2, main_2_l_0_667fbc26, main_2_l_1_7d65beac,
       main_2_l_2_df72e25f;
  wire [6:0] keyboard_1_data;
  wire [7:0] controlled_buffer_2_out, main_4_bus_out0, main_4_bus_out1, main_5_bus_out, main_6_iro,
       main_6_ram0, main_6_ram1, main_6_ram2, register_1_q;

  or or_1 (or_1_out, and_1_out, PULSE);
  and and_1 (and_1_out, HALT, ~and_2_out);  // AND_Gate
  Keyboard keyboard_1 (.clk(main_1_clk), .re(KBO), .clr(1'b0), .avail(keyboard_1_avail), .data(keyboard_1_data));
  clock_main main_1 (.HALT(1'b0), .PULSE(or_1_out), .CLK(main_1_clk), .NCLK(main_1_nclk));
  and and_2 (and_2_out, keyboard_1_avail, KBI);
  assign {controlled_buffer_1_out_2, controlled_buffer_1_out} = KBO ? {1'b0, keyboard_1_data} : 8'bz;  // Controlled_Buffer controlled_buffer_1
  or or_2 (or_2_out, KBO, COUT);
  Hex_Digit_Display hex_digit_display_1 (.value(main_2_l_2_df72e25f));  // open: dp
  BCDto7Segment_main main_2 (
    .in_1({controlled_buffer_1_out_2, controlled_buffer_1_out}), .L_0_667fbc26(main_2_l_0_667fbc26),
    .L_1_7d65beac(main_2_l_1_7d65beac), .L_2_df72e25f(main_2_l_2_df72e25f));
  assign controlled_buffer_2_out = or_2_out ? register_1_q : 8'bz;  // Controlled_Buffer controlled_buffer_2
  Register #(.trigger("high")) register_1 (
    .D({controlled_buffer_1_out_2, controlled_buffer_1_out}), .en(or_2_out), .Q(register_1_q),
    .clk(or_2_out), .clr(1'b0));
  Hex_Digit_Display hex_digit_display_2 (.value(main_2_l_1_7d65beac));  // open: dp
  Hex_Digit_Display hex_digit_display_3 (.value(main_2_l_0_667fbc26));  // open: dp
  transceiver_main main_3 (
    .BIN0(main_4_bus_out0), .BIN1(main_4_bus_out1), .AC(main_4_out_10), .BC(main_4_out_11), .ALU_O(ALU_EOUT),
    .BOUT({controlled_buffer_1_out_2, controlled_buffer_1_out}));
  REG4x8_main main_4 (
    .BUS_IN0({controlled_buffer_1_out_2, controlled_buffer_1_out}),
    .BUS_IN1({controlled_buffer_1_out_2, controlled_buffer_1_out}),
    .BUS_IN2({controlled_buffer_1_out_2, controlled_buffer_1_out}),
    .BUS_IN3({controlled_buffer_1_out_2, controlled_buffer_1_out}), .CLK(main_1_clk), .REG0(r0), .REG1(r1),
    .REG2(r2), .REG3(r3), .out_10(main_4_out_10), .out_11(main_4_out_11), .BUS_OUT0(main_4_bus_out0),
    .BUS_OUT1(main_4_bus_out1), .BUS_OUT2({controlled_buffer_1_out_2, controlled_buffer_1_out}),
    .BUS_OUT3({controlled_buffer_1_out_2, controlled_buffer_1_out}));
  // SIMPLE_ALU simple_alu_1: pin names not known; wires that end beside it: main_4_bus_out0, main_4_bus_out1, ALU_SUB, ALU_EOUT, simple_alu_1_p5[0], simple_alu_1_p5[1], {controlled_buffer_1_out_2, controlled_buffer_1_out}, IR_OUT
  PC_main main_5 (
    .CLK(main_1_nclk), .BUS_IN({controlled_buffer_1_out_2, controlled_buffer_1_out}), .PCCLR(PCCLR),
    .BUS_OUT(main_5_bus_out));  // open: IN1
  TTY #(.rows(24), .cols(80)) tty_1 (.data(controlled_buffer_2_out[6:0]), .clk(main_1_clk), .we(COUT));  // open: clr
  ALLTOGETHER_main main_6 (
    .BUSIN({controlled_buffer_1_out_2, controlled_buffer_1_out}), .C_plus_plus(CPP), .C_minus_minus(CMM),
    .CLK(main_1_clk), .BUSOUT({controlled_buffer_1_out_2, controlled_buffer_1_out}), .LR0(LR0), .LR2(LR2),
    .LRO(LRO), .RAM2(main_6_ram2), .RAM1(main_6_ram1), .RAM0(main_6_ram0), .CO(CO), .MI0(MI0), .J0(J0),
    .MI2(MI2), .J2(J2), .MII(MII), .CE(CE), .IRO(main_6_iro), .II(IR_IN));
  Register #(.width(2)) register_2 (.D(simple_alu_1_p5), .en(FI), .Q(register_2_q), .clk(main_1_clk), .clr(1'b0));
  // Probe on {controlled_buffer_1_out_2, controlled_buffer_1_out}
  RAM_main main_7 (
    .BUS1X(main_6_ram2), .BUS1M(main_6_ram1), .BUS1L(main_6_ram0), .CLK(main_1_clk),
    .DATA({controlled_buffer_1_out_2, controlled_buffer_1_out}),
    .BUSO({controlled_buffer_1_out_2, controlled_buffer_1_out}), .RI(RAM_IN), .RO(RAM_OUT));
  FW_main main_8 (
    .PC_IN(main_5_bus_out), .IR_IN(main_6_iro), .FLAG_IN(register_2_q),
    .PC_OUT({KBI, KBO, CMM, CPP, MII, LRO, LR2, LR0, CO, CE, PCCLR, RAM_OUT, RAM_IN, J2, J0, IR_IN, COUT, ALU_EOUT, ALU_SUB, HALT, MI2, MI0, FI, r3, r2, r1, r0}));
  // Probe on {controlled_buffer_1_out_2, controlled_buffer_1_out}
  LED ZERO_FLAG (.in(register_2_q[1]));
  LED CARRY_FLAG (.in(register_2_q[0]));
  Hex_Digit_Display hex_digit_display_4 (.value(controlled_buffer_1_out_2));  // open: dp
  Hex_Digit_Display hex_digit_display_5 (.value(controlled_buffer_1_out));  // open: dp
  // also tied to GND on the sheet: controlled_buffer_2_out[7]

  // Notes on the sheet:
  //   KEYBOARD
  //   80x24 LCD SCREEN
endmodule
