// Logisim project REG1.circ as structural Verilog: 1 circuit, main circuit main
module main (
  input  [7:0] IN,
  input  LOAD,
  input  CLK,
  input  SHFT,
  input  SIN,
  input  CLR,
  output SOUT,
  output [7:0] OUT
);

  Shift_Register shift_register_1 (
    .shift(SHFT), .in(SIN), .clk(CLK), .load(LOAD), .clr(CLR), .d0(IN[7]), .q0(OUT[7]), .d1(IN[6]),
    .q1(OUT[6]), .d2(IN[5]), .q2(OUT[5]), .d3(IN[4]), .q3(OUT[4]), .d4(IN[3]), .q4(OUT[3]), .d5(IN[2]),
    .q5(OUT[2]), .d6(IN[1]), .q6(OUT[1]), .d7(IN[0]), .q7(OUT[0]));  // open: out

  assign SOUT = OUT[0];
endmodule
