// Logisim project REG4x8.circ as structural Verilog: 1 circuit, main circuit main
module main (
  input  [7:0] BUS_IN0,
  input  [7:0] BUS_IN1,
  input  [7:0] BUS_IN2,
  input  [7:0] BUS_IN3,
  input  CLK,
  input  REG0,
  input  REG1,
  input  REG2,
  input  REG3,
  output out_10,
  output out_11,
  output [7:0] BUS_OUT0,
  output [7:0] BUS_OUT1,
  output [7:0] BUS_OUT2,
  output [7:0] BUS_OUT3
);

  wire AL, ASH, ASI, BL, BSH, BSI, CC, CL, CSH, CSI, DC, DL, DSH, DSI;

  ROM #(.addrWidth(4), .dataWidth(16)) rom_1 (
    .addr({REG3, REG2, REG1, REG0}),
    .data({DSI, DL, DC, DSH, CSI, CL, CC, CSH, BSI, BL, out_11, BSH, ASI, AL, out_10, ASH}), .sel(1'b1));
  // REG8_main main_1: pin names not known; wires that end beside it: CLK, ASH, out_10, ASI, AL, BUS_IN0, BUS_OUT0
  // REG8_main main_2: pin names not known; wires that end beside it: CLK, CSH, CC, CSI, CL, BUS_IN2, BUS_OUT2
  // REG8_main main_3: pin names not known; wires that end beside it: CLK, BSH, out_11, BSI, BL, BUS_IN1, BUS_OUT1
  // REG8_main main_4: pin names not known; wires that end beside it: CLK, DSH, DC, DSI, DL, BUS_IN3, BUS_OUT3

  // Other names for the same wires on the sheet: AC = out_10; BC = out_11

  // Notes on the sheet:
  //   contents of rom_1 (hex, n*v repeats v):
  //   0 20 24 26 2 42 402 4002 4 40 400 4000 200 204 240 2000
endmodule
