// Logisim project sc.circ as structural Verilog: 1 circuit, main circuit oe86
module oe86 (
  input  PULSE
);

  wire A_REG_ENABLE, ALU_EOUT, ALU_SUB, B_REG_ENABLE, CO, CU_p1, HALT, IR_IN, IR_OUT, JMP, main_1_clk,
       main_1_nclk, MI, OUTPUT_ENABLE, PROGRAM_COUNT_ENABLE, PROGRAM_COUNT_JMP, RAM_IN, RAM_OUT, REG_CLEAR,
       REG_SHIFT, REGS_p10, REGS_p11, SHIFT_IN, WRITE_ENABLE;
  wire [1:0] register_1_q, simple_alu_1_p5;
  wire [3:0] simple_alu_1_p8;
  wire [7:0] controlled_buffer_2_out, INSTRUCTION_REGISTER_q, main_2_p5, ram_1_data, REGS_p1,
       simple_alu_1_p10;

  clock_main main_1 (.HALT(HALT), .PULSE(PULSE), .CLK(main_1_clk), .NCLK(main_1_nclk));
  // reg8x2 REGS: pin names not known; wires that end beside it: REGS_p1, WRITE_ENABLE, REG_CLEAR, REG_SHIFT, SHIFT_IN, A_REG_ENABLE, main_1_clk, B_REG_ENABLE, OUTPUT_ENABLE, REGS_p10, REGS_p11
  Register INSTRUCTION_REGISTER (.D(REGS_p1), .en(JMP), .clk(main_1_nclk), .Q(INSTRUCTION_REGISTER_q), .clr(1'b0));
  // SIMPLE_ALU simple_alu_1: pin names not known; wires that end beside it: REGS_p10, REGS_p11, ALU_SUB, ALU_EOUT, simple_alu_1_p5[0], simple_alu_1_p5[1], REGS_p1, simple_alu_1_p8, {4'b0000, simple_alu_1_p8}, simple_alu_1_p10
  Controlled_Buffer #(.width(8)) controlled_buffer_1 (.en(IR_OUT));  // open: in, out
  RAM ram_1 (.addr(controlled_buffer_2_out), .we(RAM_IN), .oe(RAM_OUT), .clk(main_1_clk), .data(ram_1_data));
  // CONTROL_UNIT CU: pin names not known; wires that end beside it: CU_p1, INSTRUCTION_REGISTER_q, {RAM_OUT, RAM_IN, PROGRAM_COUNT_ENABLE, PROGRAM_COUNT_JMP, IR_IN, IR_OUT, ALU_EOUT, ALU_SUB, HALT, CO, MI, JMP, WRITE_ENABLE, OUTPUT_ENABLE, B_REG_ENABLE, A_REG_ENABLE}
  Register #(.width(2)) register_1 (.D(simple_alu_1_p5), .en(1'b1), .clk(main_1_clk), .Q(register_1_q), .clr(1'b0));
  // MAR_main main_2: pin names not known; wires that end beside it: REGS_p1, MI, main_1_clk, IR_IN, main_2_p5
  LED ZERO_FLAG (.in(register_1_q[1]));
  assign controlled_buffer_2_out = CO ? main_2_p5 : 8'bz;  // Controlled_Buffer controlled_buffer_2
  assign REGS_p1 = RAM_OUT ? ram_1_data : 8'bz;  // Controlled_Buffer controlled_buffer_3
  LED CARRY_FLAG (.in(register_1_q[0]));
endmodule
