// Logisim project ALU.circ as structural Verilog: 1 circuit, main circuit ALU
module ALU (
  input  D0,
  input  C0,
  input  B0,
  input  A0,
  input  [7:0] BUS_IN_A,
  input  [7:0] BUS_IN_B,
  input  [7:0] BUS_IN_C,
  input  [7:0] BUS_IN_D,
  input  ANDOR,
  input  DIVIDE,
  input  SUBSTRACT,
  input  SUM,
  input  O,
  output PARITY,
  output BORROW,
  output ZERO,
  output CARRY,
  output LT,
  output EQ,
  output GT,
  output [7:0] BUS_OUT
);

  wire [7:0] adder_1_out, and_1_out, divider_1_out, multiplexer_1_out, multiplexer_2_out, multiplier_1_out,
       not_1_out, or_1_out, subtractor_1_out;

  Multiplexer #(.select(4), .width(8)) multiplexer_1 (
    .in1(BUS_IN_A), .in2(BUS_IN_B), .in3(BUS_IN_A), .in4(BUS_IN_C), .in8(BUS_IN_D), .out(multiplexer_1_out),
    .sel({D0, C0, B0, A0}));  // open: in0, in5, in6, in7, in9, in10, in11, in12, in13, in14, in15
  Adder adder_1 (.a(BUS_IN_A), .b(BUS_IN_B), .out(adder_1_out), .cout(CARRY));  // open: cin
  Subtractor subtractor_1 (.a(BUS_IN_A), .b(BUS_IN_B), .out(subtractor_1_out), .bout(BORROW));  // open: bin
  Divider divider_1 (.a(BUS_IN_A), .b(BUS_IN_B), .out(divider_1_out));  // open: upper, rem
  Multiplier multiplier_1 (.a(BUS_IN_A), .b(BUS_IN_B), .out(multiplier_1_out));  // open: cin, cout
  Comparator comparator_1 (.a(BUS_IN_A), .b(BUS_IN_B), .gt(LT), .eq(EQ), .lt(GT));
  assign not_1_out = ~BUS_IN_A;  // NOT_Gate not_1, 8 bits wide
  assign and_1_out = BUS_IN_A & BUS_IN_B;  // AND_Gate and_1, 8 bits wide
  assign or_1_out = BUS_IN_A | BUS_IN_B;  // OR_Gate or_1, 8 bits wide
  Multiplexer #(.enable("true"), .select(4), .width(8)) multiplexer_2 (
    .in0(multiplexer_1_out), .in1(adder_1_out), .in2(subtractor_1_out), .in3(not_1_out), .in4(divider_1_out),
    .in5(multiplier_1_out), .in9(and_1_out), .in10(or_1_out), .out(multiplexer_2_out),
    .sel({ANDOR, DIVIDE, SUBSTRACT, SUM}), .en(O));  // open: in6, in7, in8, in11, in12, in13, in14, in15
  assign BUS_OUT = O ? multiplexer_2_out : 8'bz;  // Controlled_Buffer controlled_buffer_1
  nor nor_1 (ZERO, multiplexer_2_out[0], multiplexer_2_out[1], multiplexer_2_out[2], multiplexer_2_out[3], multiplexer_2_out[4], multiplexer_2_out[5], multiplexer_2_out[6], multiplexer_2_out[7]);
  not not_2 (PARITY, multiplexer_2_out[0]);
endmodule
