// Logisim project Clock_C.circ as structural Verilog: 1 circuit, main circuit Clock_c
module Clock_c (
  input  HALT,
  input  PULSE,
  output CLK,
  output NCLK
);

  wire and_1_out, clock_1_out;

  Clock clock_1 (.out(clock_1_out));
  and and_1 (and_1_out, clock_1_out, ~HALT);  // AND_Gate
  or or_1 (CLK, and_1_out, PULSE);
  not not_1 (NCLK, CLK);
endmodule
