// Logisim project MAINBOARD.circ as structural Verilog: 1 circuit, main circuit main
module main (
  input  Input_1,
  input  [7:0] Input_bus_1
);

  wire A, A0, and_1_out, and_6_out, and_7_out, and_8_out, and_9_out, B, B0, C, C0, CE, CL, Clock_c_1_nclk,
       CMM, CO, comparator_1_eq, comparator_2_eq, controlled_buffer_1_out, controlled_buffer_2_out,
       controlled_buffer_3_out, controlled_buffer_4_out, controlled_buffer_5_out, controlled_buffer_7_out,
       controlled_buffer_8_out, controlled_buffer_9_out, controlled_buffer_10_out, controlled_buffer_11_out,
       controlled_buffer_12_out, controlled_buffer_14_out, controlled_buffer_15_out,
       controlled_buffer_16_out, controlled_buffer_17_out, controlled_buffer_18_out,
       controlled_buffer_19_out, controlled_buffer_20_out, controlled_buffer_21_out,
       controlled_buffer_22_out, COUT, CPP, D, D0, DIV, E0, FI, HALT, II, JMP, KBI, KBO, keyboard_1_avail,
       LD, LR0, LR2, LRS, LRW, MI, O, or_1_out, or_2_out, or_3_out, PC_CLR, POKE, RO, RST, RW, S0, SHIN,
       SHOUT, SIN, SUB, telnet_1_p5;
  wire [3:0] STACK_1_buso, STACK_1_buso_2;
  wire [6:0] ALU_1_parity, keyboard_1_data;
  wire [6:4] FLAGS_q_2;
  wire [7:0] controlled_buffer_13_out, controlled_buffer_23_out, IR_1_fwo, MAR_1_bout1, MAR_1_bout2,
       MAR_1_bout3, MAR_1_bout4, Program_Counter_1_bout1, Program_Counter_1_bout2, Program_Counter_1_bout3,
       Program_Counter_1_bout4, RAM_1_dout, REG8_1_bout, REG8_2_bout, REG8_3_bout, REG8_4_bout, register_1_q,
       SC_1_bout1, telnet_1_p4;
  wire [15:0] counter_1_q;
  wire [19:16] FLAGS_q;

  Hex_Digit_Display Hex_Digit_Display_1 (.value(STACK_1_buso_2));  // open: dp
  Keyboard #(.buflen(256)) keyboard_1 (
    .clk(Clock_c_1_nclk), .re(and_1_out), .clr(1'b0), .avail(keyboard_1_avail), .data(keyboard_1_data));
  or or_1 (or_1_out, and_1_out, HALT);
  Hex_Digit_Display Hex_Digit_Display_2 (.value(STACK_1_buso));  // open: dp
  Clock_c Clock_c_1 (.HALT(or_1_out), .PULSE(Input_1), .NCLK(Clock_c_1_nclk));  // open: NO, CLK
  STACK STACK_1 (
    .COUNTER_IN({STACK_1_buso_2, STACK_1_buso}), .DATA({STACK_1_buso_2, STACK_1_buso}), .CLK(Clock_c_1_nclk),
    .LRS(LRS), .LR2(LR2), .LR0(LR0), .LRW(LRW), .CPP(CPP), .CMM(CMM), .BUSO({STACK_1_buso_2, STACK_1_buso}));
  REG8 REG8_1 (
    .BIN({STACK_1_buso_2, STACK_1_buso}), .CLK(Clock_c_1_nclk), .LDL(controlled_buffer_5_out),
    .CLL(controlled_buffer_4_out), .SIN(controlled_buffer_3_out), .S0(controlled_buffer_2_out),
    .OP(controlled_buffer_1_out), .BOUT(REG8_1_bout));  // open: SOUT
  assign controlled_buffer_1_out = A ? O : 1'bz;  // Controlled_Buffer controlled_buffer_1
  assign controlled_buffer_2_out = A ? S0 : 1'bz;  // Controlled_Buffer controlled_buffer_2
  assign controlled_buffer_3_out = A ? SIN : 1'bz;  // Controlled_Buffer controlled_buffer_3
  assign controlled_buffer_4_out = A ? CL : 1'bz;  // Controlled_Buffer controlled_buffer_4
  assign controlled_buffer_5_out = A ? LD : 1'bz;  // Controlled_Buffer controlled_buffer_5
  assign {STACK_1_buso_2, STACK_1_buso} = KBI ? {1'b0, keyboard_1_data} : 8'bz;  // Controlled_Buffer controlled_buffer_6
  and and_1 (and_1_out, keyboard_1_avail, HALT, KBI);
  Program_Counter Program_Counter_1 (
    .BIN1({STACK_1_buso_2, STACK_1_buso}), .CLK(Clock_c_1_nclk), .SHIN(SHIN), .CE(CE), .JMP(JMP), .RST(RST),
    .CO(CO), .SHOUT(SHOUT), .BOUT1(Program_Counter_1_bout1), .BOUT2(Program_Counter_1_bout2),
    .BOUT3(Program_Counter_1_bout3), .BOUT4(Program_Counter_1_bout4), .BOUTS({STACK_1_buso_2, STACK_1_buso}));  // open: ERR
  and and_2 (A0, O, A);
  and and_3 (B0, O, B);
  and and_4 (C0, O, C);
  and and_5 (D0, O, D);
  REG8 REG8_2 (
    .BIN({STACK_1_buso_2, STACK_1_buso}), .CLK(Clock_c_1_nclk), .LDL(controlled_buffer_11_out),
    .CLL(controlled_buffer_10_out), .SIN(controlled_buffer_9_out), .S0(controlled_buffer_8_out),
    .OP(controlled_buffer_7_out), .BOUT(REG8_2_bout));  // open: SOUT
  assign controlled_buffer_7_out = B ? O : 1'bz;  // Controlled_Buffer controlled_buffer_7
  assign controlled_buffer_8_out = B ? S0 : 1'bz;  // Controlled_Buffer controlled_buffer_8
  assign controlled_buffer_9_out = B ? SIN : 1'bz;  // Controlled_Buffer controlled_buffer_9
  assign controlled_buffer_10_out = B ? CL : 1'bz;  // Controlled_Buffer controlled_buffer_10
  REG8 REG8_3 (
    .BIN({STACK_1_buso_2, STACK_1_buso}), .CLK(Clock_c_1_nclk), .LDL(controlled_buffer_17_out),
    .CLL(controlled_buffer_16_out), .SIN(controlled_buffer_15_out), .S0(controlled_buffer_14_out),
    .OP(controlled_buffer_12_out), .BOUT(REG8_3_bout));  // open: SOUT
  assign controlled_buffer_11_out = B ? LD : 1'bz;  // Controlled_Buffer controlled_buffer_11
  assign controlled_buffer_12_out = C ? O : 1'bz;  // Controlled_Buffer controlled_buffer_12
  assign controlled_buffer_13_out = C ? {STACK_1_buso_2, STACK_1_buso} : 8'bz;  // Controlled_Buffer controlled_buffer_13
  MAR MAR_1 (
    .BIN1(Program_Counter_1_bout1), .BIN2(Program_Counter_1_bout2), .BIN3(Program_Counter_1_bout3),
    .BIN4(Program_Counter_1_bout4), .CLK(Clock_c_1_nclk), .MI(MI), .BOUT1(MAR_1_bout1), .BOUT2(MAR_1_bout2),
    .BOUT3(MAR_1_bout3), .BOUT4(MAR_1_bout4));
  assign controlled_buffer_14_out = C ? S0 : 1'bz;  // Controlled_Buffer controlled_buffer_14
  assign controlled_buffer_15_out = C ? SIN : 1'bz;  // Controlled_Buffer controlled_buffer_15
  assign controlled_buffer_16_out = C ? CL : 1'bz;  // Controlled_Buffer controlled_buffer_16
  assign controlled_buffer_17_out = C ? LD : 1'bz;  // Controlled_Buffer controlled_buffer_17
  Register #(.trigger("high")) register_1 (
    .D({STACK_1_buso_2, STACK_1_buso}), .en(COUT), .Q(register_1_q), .clk(COUT), .clr(1'b0));
  and and_6 (and_6_out, A, POKE);
  and and_7 (and_7_out, B, POKE);
  and and_8 (and_8_out, POKE, C);
  ALU ALU_1 (
    .BUS_IN_A(REG8_1_bout), .BUS_IN_B(REG8_2_bout), .BUS_IN_C(REG8_3_bout), .BUS_IN_D(REG8_4_bout),
    .ANDOR(1'b0), .DIVIDE(DIV), .SUBSTRACT(SUB), .SUM(E0), .O(O), .D0(D0), .C0(C0), .B0(B0), .A0(A0),
    .PARITY(ALU_1_parity[0]), .BORROW(ALU_1_parity[1]), .CARRY(ALU_1_parity[3]), .LT(ALU_1_parity[4]),
    .EQ(ALU_1_parity[5]), .GT(ALU_1_parity[6]), .BUS_OUT({STACK_1_buso_2, STACK_1_buso}));  // open: ZERO
  REG8 REG8_4 (
    .BIN({STACK_1_buso_2, STACK_1_buso}), .CLK(Clock_c_1_nclk), .LDL(controlled_buffer_22_out),
    .CLL(controlled_buffer_21_out), .SIN(controlled_buffer_20_out), .S0(controlled_buffer_19_out),
    .OP(controlled_buffer_18_out), .BOUT(REG8_4_bout));  // open: SOUT
  assign controlled_buffer_18_out = D ? O : 1'bz;  // Controlled_Buffer controlled_buffer_18
  assign controlled_buffer_19_out = D ? S0 : 1'bz;  // Controlled_Buffer controlled_buffer_19
  assign controlled_buffer_20_out = D ? SIN : 1'bz;  // Controlled_Buffer controlled_buffer_20
  assign controlled_buffer_21_out = D ? CL : 1'bz;  // Controlled_Buffer controlled_buffer_21
  assign controlled_buffer_22_out = D ? LD : 1'bz;  // Controlled_Buffer controlled_buffer_22
  assign controlled_buffer_23_out = COUT ? register_1_q : 8'bz;  // Controlled_Buffer controlled_buffer_23
  Comparator #(.width(7)) comparator_1 (
    .a(controlled_buffer_23_out[6:0]), .b(7'b0001100), .eq(comparator_1_eq));  // open: gt, lt
  or or_2 (or_2_out, and_7_out, and_8_out);
  RAM #(.addrWidth(16), .trigger("high")) RAM_1 (
    .addr(counter_1_q), .we(and_8_out), .oe(Clock_c_1_nclk), .din(controlled_buffer_13_out), .dout(RAM_1_dout));
  RAM_C ram_c_1 (
    .ADDR1(MAR_1_bout1), .ADDR2(MAR_1_bout2), .ADDR3(MAR_1_bout3), .ADDR4(MAR_1_bout4),
    .DATA({STACK_1_buso_2, STACK_1_buso}), .CLK(Clock_c_1_nclk), .ROE(RO), .RWE(RW),
    .BOUT({STACK_1_buso_2, STACK_1_buso}));
  assign {STACK_1_buso_2, STACK_1_buso} = and_9_out ? telnet_1_p4 : 8'bz;  // Controlled_Buffer controlled_buffer_24
  Counter #(.max('hfb)) counter_1 (
    .load(and_6_out), .D({STACK_1_buso_2, STACK_1_buso}), .Q(counter_1_q[7:0]), .clk(or_3_out));  // open: count, carry, up, clr
  or or_3 (or_3_out, and_6_out, and_8_out);
  Counter #(.max('hfb)) counter_2 (
    .load(and_7_out), .D({STACK_1_buso_2, STACK_1_buso}), .count(comparator_2_eq), .Q(counter_1_q[15:8]),
    .up(comparator_2_eq), .clk(or_2_out));  // open: carry, clr
  SC SC_1 (.BIN1({STACK_1_buso_2, STACK_1_buso}), .PCCLR(PC_CLR), .CLK(Clock_c_1_nclk), .BOUT1(SC_1_bout1));
  IR IR_1 (.FWI({STACK_1_buso_2, STACK_1_buso}), .CLK(Clock_c_1_nclk), .INSI(II), .FWO(IR_1_fwo));
  // Telnet #(.buflen(1048576), .port(6667)) telnet_1: pin names not known; wires that end beside it: {STACK_1_buso_2, STACK_1_buso}, Clock_c_1_nclk, KBI, telnet_1_p4, telnet_1_p5, COUT
  and and_9 (and_9_out, telnet_1_p5, KBO);
  TTY #(.cols(80), .rows(24)) tty_1 (
    .data(controlled_buffer_23_out[6:0]), .clk(Clock_c_1_nclk), .we(COUT), .clr(comparator_1_eq));
  Comparator #(.mode("unsigned")) comparator_2 (.a(counter_1_q[7:0]), .b(8'hfb), .eq(comparator_2_eq));  // open: gt, lt
  // RGB_Video #(.height(256), .width(256)) rgb_video_1: pin names not known; wires that end beside it: comparator_1_eq, and_8_out, and_8_out, counter_1_q[7:0], counter_1_q[15:8], RAM_1_dout
  Register #(.trigger("low"), .width(7)) FLAGS (
    .D(ALU_1_parity), .en(FI), .Q({FLAGS_q_2, FLAGS_q}), .clk(Clock_c_1_nclk), .clr(1'b0));
  ROM #(.addrWidth(20), .dataWidth(35)) rom_1 (
    .addr({FLAGS_q, IR_1_fwo, SC_1_bout1}),
    .data({PC_CLR, POKE, HALT, COUT, FI, O, II, SHOUT, KBO, KBI, E0, SUB, DIV, CMM, CPP, LRS, LR2, LR0, LRW, SHIN, CE, CO, RST, JMP, RO, RW, MI, S0, SIN, CL, LD, D, C, B, A}));
  LED PARITY (.in(FLAGS_q[16]));
  LED BORROW (.in(FLAGS_q[17]));
  LED ZERO (.in(FLAGS_q[18]));
  LED CARRY (.in(FLAGS_q[19]));
  LED LESSER (.in(FLAGS_q_2[4]));
  LED EQUAL (.in(FLAGS_q_2[5]));
  LED GREATER (.in(FLAGS_q_2[6]));

  // Notes on the sheet:
  //   contents of rom_1 (hex, n*v repeats v):
  //   2500 10004400 2500 10004400 2500 10004400 2500 10004400 2500 10004400 2500 10004400 2500 10004400
  //   2500 10004400 2500 10004400 2500 10004400 2500 10004400 2500 10004400 2500 10004400 2500 10004400
  //   2500 10004400 2500 10004400 2500 10004400 2500 10004400 2500 10004400 2500 10004400 2500 10004400
  //   2500 10004400 2500 10004400 2500 10004400 2500 10004400 2500 10004400 2500 10004400 2500 10004400
  //   2500 10004400 2500 10004400 2500 10004400 2500 10004400 2500 10004400 2500 10004400 2500 10004400
  //   2500 10004400 2500 10004400 2500 10004400 2500 10004400 2500 10004400 2500 10004400 2500 10004400
  //   2500 10004400 2500 10004400 2500 10004400 2500 10004400 2500 10004400 2500 10004400 2500 10004400
  //   2500 10004400 2500 10004400 2500 10004400 2500 10004400 2500 10004400 2500 10004400 2500 10004400
  //   2500 10004400 2500 10004400 2500 10004400 2500 10004400 2500 10004400 2500 10004400 2500 10004400
  //   2500 10004400 2500 10004400 2500 10004400 2500 10004400 2500 10004400 2500 10004400 2500 10004400
  //   2500 10004400 2500 10004400 2500 10004400 2500 10004400 2500 10004400 2500 10004400 2500 10004400
  //   2500 10004400 2500 10004400 2500 10004400 2500 10004400 2500 10004400 2500 10004400 2500 10004400
  //   2500 10004400 2500 10004400 2500 10004400 2500 10004400 2500 10004400 2500 10004400 2500 10004400
  //   2500 10004400 2500 10004400 2500 10004400 2500 10004400 2500 10004400 2500 10004400 2500 10004400
  //   2500 10004400 2500 10004400 2500 10004400 2500 10004400 2500 10004400 2500 10004400 2500 10004400
  //   2500 10004400 2500 10004400 2500 10004400 2500 10004400 2500 10004400 2500 10004400 2500 10004400
  //   2500 10004400 2500 10004400 2500 10004400 2500 10004400 2500 10004400 2500 10004400 2500 10004400
  //   2500 10004400 2500 10004400 2500 10004400 2500 10004400 2500 10004400 2500 10004400 2500 10004400
  //   2500 10004400 2500 10004400 2500 10004400 80011 20300001 400000000 10004400 2500 10004400 2500
  //   10004400 2500 10004400 2500 10004400 2500 10004400 2500 10004400 2500 10004400 2500 10004400 2500
  //   10004400 2500 10004400 2500 10004400 2500 10004400 2500 10004400 2500 10004400 2500 10004400 2500
  //   10004400 2500 10004400 2500 10004400 2500 10004400 2500 10004400 2500 10004400 2500 10004400 2500
  //   10004400 2500 10004400 2500 10004400 2500 10004400 2500 10004400 2500 10004400 2500 10004400 2500
  //   10004400 2500 10004400 2500 10004400 2500 10004400 2500 10004400 2500 10004400 2500 10004400 2500
  //   10004400 2500 10004400 2500 10004400 2500 10004400 2500 10004400 2500 10004400 2500 10004400 2500
  //   10004400 2500 10004400 2500 10004400 2500 10004400 2500 10004400 2500 10004400 2500 10004400 2500
  //   10004400 2500 10004400 2500 10004400 2500 10004400 2500 10004400 2500 10004400 2500 10004400 2500
  //   10004400 2500 10004400 2500 10004400 2500 10004400 2500 10004400 2500 10004400 2500 10004400 2500
  //   10004400 2500 10004400 2500 10004400 2500 10004400 2500 10004400 2500 10004400 2500 10004400 2500
  //   10004400 2500 10004400 2500 10004400 2500 10004400 2500 10004400 2500 10004400 2500 10004400 2500
  //   10004400 2500 10004400 2500 10004400 2500 10004400 2500 10004400 2500 10004400 2500 10004400 2500
  //   10004400 2500 10004400 2500 10004400 2500 10004400 2500 10004400 2500 10004400 2500 10004400 2500
  //   10004400 2500 10004400 2500 10004400 2500 10004400 2500 10004400 2500 10004400 2500 10004400 2500
  //   10004400 2500 10004400 2500 10004400 2500 10004400 2500 10004400 2500 10004400 2500 10004400 2500
  //   10004400 2500 10004400 2500 10004400 2500 10004400 2500 10004400 2500 10004400 2500 10004400 2500
  //   10004400 2500 10004400 2500 10004400 2500 10004400 2500 10004400 2500 10004400 2500 10004400 2500
  //   10004400 2500 10004400 2500 10004400 2500 10004400 2500 10004400 2500 10004400 2500 10004400 2500
  //   10004400 2500 10004400 2500 10004400 2500 10004400 2500 10004400 2500 10004400 2500 10004400 2500
  //   10004400 2500 10004400 2500 10004400 2500 10004400 2500 10004400 2500 10004400 2500 10004400 2500
  //   10004400 2500 10004400 2500 10004400 2500 10004400 2500 10004400 2500 10004400 2500 10004400 2500
  //   10004400 2500 10004400 2500 10004400 2500 10004400 2500 10004400 2500 10004400 2500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
endmodule
