// Logisim project Memory_C.circ as structural Verilog: 1 circuit, main circuit RAM_C
// RAM
module RAM_C (
  input  CLK,
  input  ROE,
  input  RWE,
  input  [7:0] ADDR1,
  input  [7:0] ADDR2,
  input  [7:0] ADDR3,
  input  [7:0] ADDR4,
  input  [7:0] DATA,
  output [7:0] BOUT
);

  wire [7:0] MEM0_dout;

  RAM #(.addrWidth(32), .trigger("high"), .\type ("nonvolatile")) MEM0 (
    .addr({ADDR4, ADDR3, ADDR2, ADDR1}), .we(RWE), .oe(ROE), .clk(CLK), .din(DATA), .dout(MEM0_dout));
  assign BOUT = ROE ? MEM0_dout : 8'bz;  // Controlled_Buffer controlled_buffer_1
endmodule
