// Logisim project REG1.circ as structural Verilog: 1 circuit, main circuit main
module main (
  input  [7:0] IN,
  input  LOAD,
  input  CLK,
  input  SHFT,
  input  SIN,
  input  CLR,
  output SOUT,
  output [7:0] out_8
);

  Register register_1 (.D(IN), .en(LOAD), .clk(CLK), .Q(out_8), .clr(CLR));
endmodule
