// Logisim project STACK2.circ as structural Verilog: 1 circuit, main circuit STACK
module STACK (
  input  [7:0] COUNTER_IN,
  input  CPP,
  input  CMM,
  input  CLK,
  input  [7:0] DATA,
  input  LRS,
  input  LR2,
  input  LR0,
  input  LRW,
  output [7:0] BUSO
);

  wire and_1_out, and_2_out, and_3_out, and_4_out, decoder_1_out1, decoder_1_out2, decoder_1_out3,
       decoder_2_out0, decoder_2_out9, decoder_2_out10, decoder_2_out11, decoder_2_out12, decoder_2_out13,
       decoder_2_out14, decoder_2_out15, multiplexer_1_out, multiplexer_3_p5, not_1_out, not_2_out, or_1_out,
       undriven, undriven_2, undriven_3, undriven_4, undriven_5, undriven_6, undriven_7, undriven_8;
  wire [7:0] controlled_buffer_1_out, controlled_buffer_2_out, controlled_buffer_3_out,
       controlled_buffer_5_out, counter_1_q, counter_2_q, multiplexer_2_out, ram_1_dout, ram_2_dout,
       ram_3_dout, ram_4_dout;

  not not_1 (not_1_out, LRS);
  Decoder #(.select(2)) decoder_1 (
    .out1(decoder_1_out1), .out2(decoder_1_out2), .out3(decoder_1_out3), .sel({CPP, CMM}), .en(1'b1));  // open: out0
  Multiplexer multiplexer_1 (.in0(decoder_1_out1), .in1(decoder_1_out2), .out(multiplexer_1_out), .sel(decoder_1_out2));
  and and_1 (and_1_out, decoder_1_out3, LRS);
  and and_2 (and_2_out, decoder_1_out2, LRS);
  and and_3 (and_3_out, decoder_1_out1, LRS);
  and and_4 (and_4_out, not_1_out, multiplexer_1_out);
  Counter counter_1 (
    .load(and_1_out), .D(COUNTER_IN), .count(or_1_out), .Q(counter_1_q), .up(and_2_out), .clk(CLK), .clr(1'b0));  // open: carry
  or or_1 (or_1_out, and_2_out, and_3_out);
  Counter counter_2 (
    .load(1'b0), .D(COUNTER_IN), .count(and_4_out), .Q(counter_2_q), .up(decoder_1_out2), .clk(CLK),
    .clr(1'b0));  // open: carry
  Decoder #(.enable("false"), .select(4)) decoder_2 (
    .out0(decoder_2_out0), .out9(decoder_2_out9), .out10(decoder_2_out10), .out11(decoder_2_out11),
    .out12(decoder_2_out12), .out13(decoder_2_out13), .out14(decoder_2_out14), .out15(decoder_2_out15),
    .sel({LRS, LRW, LR2, LR0}));  // open: out1, out2, out3, out4, out5, out6, out7, out8
  Multiplexer #(.width(8)) multiplexer_2 (.in0(counter_2_q), .in1(counter_1_q), .out(multiplexer_2_out), .sel(LRS));
  RAM #(.asyncread("true")) ram_1 (
    .addr(multiplexer_2_out), .we(undriven), .oe(undriven), .clk(CLK), .din(DATA), .dout(ram_1_dout));
  assign controlled_buffer_1_out = undriven_2 ? ram_1_dout : 8'bz;  // Controlled_Buffer controlled_buffer_1
  RAM #(.asyncread("true")) ram_2 (
    .addr(multiplexer_2_out), .we(undriven_3), .oe(undriven_4), .clk(CLK), .din(DATA), .dout(ram_2_dout));
  not not_2 (not_2_out, LRW);
  assign controlled_buffer_2_out = undriven_4 ? ram_2_dout : 8'bz;  // Controlled_Buffer controlled_buffer_2
  RAM #(.asyncread("true")) ram_3 (
    .addr(multiplexer_2_out), .we(undriven_5), .oe(undriven_6), .clk(CLK), .din(DATA), .dout(ram_3_dout));
  assign controlled_buffer_3_out = undriven_6 ? ram_3_dout : 8'bz;  // Controlled_Buffer controlled_buffer_3
  RAM #(.asyncread("true")) ram_4 (
    .addr(multiplexer_2_out), .we(undriven_7), .oe(undriven_8), .clk(CLK), .din(DATA), .dout(ram_4_dout));
  Controlled_Buffer #(.width(8)) controlled_buffer_4 (.in(multiplexer_2_out), .en(decoder_2_out0));  // open: out
  assign controlled_buffer_5_out = undriven_8 ? ram_4_dout : 8'bz;  // Controlled_Buffer controlled_buffer_5
  // Multiplexer #(.enable("true"), .select(4), .width(8)) multiplexer_3: pin names not known; wires that end beside it: controlled_buffer_5_out, controlled_buffer_3_out, controlled_buffer_2_out, controlled_buffer_1_out, multiplexer_3_p5, {LRW, LR2, LR0}, not_2_out, BUSO
endmodule
