// Logisim project Step_Counter.circ as structural Verilog: 1 circuit, main circuit SC
module SC (
  input  PCCLR,
  input  [7:0] BIN1,
  input  CLK,
  output [7:0] BOUT1
);

  Counter counter_1 (.load(1'b0), .D(BIN1), .count(CLK), .Q(BOUT1), .up(CLK), .clk(CLK), .clr(PCCLR));  // open: carry
endmodule
